// Logisim project 21052018.circ as structural Verilog: 1 circuit, main circuit main
module main (
  input  R,
  input  S,
  input  S_2,
  input  R_2,
  input  S_3,
  input  R_3,
  input  S_4,
  input  S_5,
  input  CLK,
  input  CLK_2,
  input  R_4,
  input  R_5,
  input  D,
  input  CLK_3,
  input  D_2,
  input  CLK_4,
  input  S_6,
  input  CLK_5,
  input  R_6,
  input  in_20,
  input  in_21,
  input  in_22,
  input  in_23,
  input  CLK_6,
  input  CLK_7,
  input  S_7,
  input  CLK_8,
  input  R_7,
  input  in_29,
  input  CLK_9,
  input  in_31,
  output Q,
  output Q_2,
  output Q_3,
  output Q_4,
  output Q_5,
  output Q_6,
  output Q_7,
  output Q_8,
  output Q_9,
  output Q_10,
  output Q_11,
  output Q_12,
  output Q_13,
  output Q_14,
  output Q_15,
  output Q_16,
  output Q_17,
  output Q_18,
  output Q_19,
  output Q_20,
  output out_52,
  output out_53,
  output Q_21,
  output Q_22,
  output Q_23,
  output Q_24,
  output Q_25,
  output Q_26,
  output Q_27,
  output Q_28,
  output Q_29,
  output Q_30,
  output Q_31,
  output Q_32,
  output Q_33,
  output Q_34,
  output Q_35,
  output Q_36
);

  wire and_1_out, and_2_out, and_3_out, and_4_out, clock_1_out, nand_3_out, nand_6_out, nand_7_out,
       nand_10_out, nand_11_out, nand_12_out, nand_13_out, nand_14_out, nand_19_out, nand_20_out,
       nand_23_out, nand_24_out, nand_25_out, nand_26_out, nand_27_out, nand_28_out, nand_29_out,
       nand_30_out, nand_37_out, nand_38_out, nand_41_out, nand_42_out, nand_47_out, nand_48_out,
       nand_49_out, nand_50_out, nand_51_out, nand_52_out, nand_59_out, nand_60_out, nand_63_out,
       nand_64_out, not_1_out, not_2_out, not_3_out, not_4_out, not_5_out, not_6_out, not_7_out, not_8_out,
       not_9_out, not_10_out, not_11_out, not_12_out, not_13_out;

  not not_1 (not_1_out, D);
  not not_2 (not_2_out, D_2);
  nor nor_1 (Q, R, Q_2);
  nor nor_2 (Q_2, Q, S);
  nand nand_1 (Q_3, S_2, Q_4);
  nand nand_2 (Q_4, Q_3, R_2);
  nand nand_3 (nand_3_out, S_3, S_3);
  nand nand_4 (Q_5, nand_3_out, Q_6);
  nand nand_5 (Q_6, Q_5, nand_6_out);
  nand nand_6 (nand_6_out, R_3, R_3);
  nand nand_7 (nand_7_out, S_4, CLK);
  nand nand_8 (Q_7, nand_7_out, Q_9);
  nand nand_9 (Q_9, Q_7, nand_10_out);
  nand nand_10 (nand_10_out, CLK, R_4);
  nand nand_11 (nand_11_out, D, CLK_3);
  nand nand_12 (nand_12_out, CLK_3, not_1_out);
  nand nand_13 (nand_13_out, D_2, CLK_4);
  nand nand_14 (nand_14_out, CLK_4, not_2_out);
  Clock clock_1 (.out(clock_1_out));
  nand nand_15 (Q_11, nand_11_out, Q_12);
  nand nand_16 (Q_12, Q_11, nand_12_out);
  nand nand_17 (Q_13, nand_13_out, Q_15);
  nand nand_18 (Q_15, Q_13, nand_14_out);
  nand nand_19 (nand_19_out, S_6, ~R_6, CLK_5);  // NAND_Gate
  nand nand_20 (nand_20_out, CLK_5, ~S_6, R_6);  // NAND_Gate
  not not_3 (not_3_out, CLK_4);
  nand nand_21 (Q_17, nand_19_out, Q_19);
  nand nand_22 (Q_19, Q_17, nand_20_out);
  not not_4 (not_4_out, Q_28);
  and and_1 (and_1_out, CLK_6, clock_1_out);
  and and_2 (and_2_out, Q_36, in_29);
  and and_3 (and_3_out, in_31, Q_34);
  not not_5 (not_5_out, Q_13);
  not not_6 (not_6_out, CLK_5);
  nand nand_23 (nand_23_out, Q_28, and_1_out);
  nand nand_24 (nand_24_out, and_1_out, not_4_out);
  nand nand_25 (nand_25_out, Q_32, ~Q_30, CLK_8);  // NAND_Gate
  nand nand_26 (nand_26_out, CLK_8, ~Q_32, Q_30);  // NAND_Gate
  nand nand_27 (nand_27_out, and_2_out, ~and_3_out, CLK_9);  // NAND_Gate
  nand nand_28 (nand_28_out, CLK_9, ~and_2_out, and_3_out);  // NAND_Gate
  nand nand_29 (nand_29_out, Q_13, not_3_out);
  nand nand_30 (nand_30_out, not_3_out, not_5_out);
  nand nand_31 (Q_23, nand_23_out, Q_27);
  nand nand_32 (Q_27, Q_23, nand_24_out);
  nand nand_33 (Q_29, nand_25_out, Q_31);
  nand nand_34 (Q_31, Q_29, nand_26_out);
  nand nand_35 (Q_33, nand_27_out, Q_35);
  nand nand_36 (Q_35, Q_33, nand_28_out);
  nand nand_37 (nand_37_out, S_5, ~R_5, CLK_2);  // NAND_Gate
  nand nand_38 (nand_38_out, CLK_2, ~S_5, R_5);  // NAND_Gate
  nand nand_39 (Q_14, nand_29_out, Q_16);
  nand nand_40 (Q_16, Q_14, nand_30_out);
  nand nand_41 (nand_41_out, Q_17, ~Q_19, not_6_out);  // NAND_Gate
  nand nand_42 (nand_42_out, not_6_out, ~Q_17, Q_19);  // NAND_Gate
  not not_7 (not_7_out, and_1_out);
  not not_8 (not_8_out, CLK_8);
  not not_9 (not_9_out, CLK_9);
  nand nand_43 (Q_8, nand_37_out, Q_10);
  nand nand_44 (Q_10, Q_8, nand_38_out);
  nand nand_45 (Q_18, nand_41_out, Q_20);
  nand nand_46 (Q_20, Q_18, nand_42_out);
  not not_10 (not_10_out, Q_23);
  nand nand_47 (nand_47_out, Q_23, not_7_out);
  nand nand_48 (nand_48_out, not_7_out, not_10_out);
  nand nand_49 (nand_49_out, Q_29, ~Q_31, not_8_out);  // NAND_Gate
  nand nand_50 (nand_50_out, not_8_out, ~Q_29, Q_31);  // NAND_Gate
  nand nand_51 (nand_51_out, Q_33, ~Q_35, not_9_out);  // NAND_Gate
  nand nand_52 (nand_52_out, not_9_out, ~Q_33, Q_35);  // NAND_Gate
  nand nand_53 (Q_24, nand_47_out, Q_28);
  nand nand_54 (Q_28, Q_24, nand_48_out);
  nand nand_55 (Q_30, nand_49_out, Q_32);
  nand nand_56 (Q_32, Q_30, nand_50_out);
  nand nand_57 (Q_34, nand_51_out, Q_36);
  nand nand_58 (Q_36, Q_34, nand_52_out);
  T_Flip_Flop #(.trigger("falling")) t_ff_1 (.T(in_20), .clk(in_21), .Q(out_53));  // open: Qn, reset, preset
  not not_11 (not_11_out, Q_26);
  and and_4 (and_4_out, CLK_7, Q_24);
  nand nand_59 (nand_59_out, Q_26, and_4_out);
  nand nand_60 (nand_60_out, and_4_out, not_11_out);
  T_Flip_Flop #(.trigger("falling")) t_ff_2 (.T(out_53), .clk(in_21), .Q(out_52));  // open: Qn, reset, preset
  nand nand_61 (Q_21, nand_59_out, Q_25);
  nand nand_62 (Q_25, Q_21, nand_60_out);
  not not_12 (not_12_out, and_4_out);
  not not_13 (not_13_out, Q_21);
  nand nand_63 (nand_63_out, Q_21, not_12_out);
  nand nand_64 (nand_64_out, not_12_out, not_13_out);
  nand nand_65 (Q_22, nand_63_out, Q_26);
  nand nand_66 (Q_26, Q_22, nand_64_out);
  // Buffer buffer_1 is placed but not wired

  // Notes on the sheet:
  //   _
  //   _
  //   Przerzutnik RS
  //   Dwie jedynki na wejściu - stan oczekiwania
  //   Oszukany RS na NANDach
  //   Synchroniczny RS
  //   Przerzutnik D (aktywowany zboczem)
  //   Stan zabroniony - dwa zera na wyjściu (logika się psuje)
  //   Przerzutnik D (zatrzaskiwany zboczem)
  //   _
  //   _
  //   _
  //   _
  //   _
  //   _
  //   Przerzutnik RS (zatrzaskiwany zboczem)
  //   _
  //   Przerzutnik JK (zastępuje RS i T, lub też D)
  //   Synchroniczny RS bez stanu zabronionego
  //   _
  //   Przerzutnik T z RS synchronicznego
  //   Przerzutnik T (niepełny) (dzielnik częstotliwości) (licznik)
  //   _
  //   _
  //   _
  //   _
  //   _
  //   _
  //   _
  //   _
  //   Przerzutnik T (niepełny) (dzielnik częstotliwości) (licznik)
  //   _
  //   _
endmodule
