// Logisim project DM74138.circ as structural Verilog: 1 circuit, main circuit main
module main (
  input  in_1,
  input  in_2,
  input  in_3,
  input  in_4,
  input  in_5,
  input  in_6,
  input  in_7,
  input  in_8,
  input  in_9,
  input  in_10,
  input  [2:0] in_11,
  input  [2:0] in_12,
  input  in_13,
  input  in_14,
  input  in_15,
  input  in_16,
  input  in_17,
  input  in_18,
  input  in_19,
  input  in_20,
  input  in_21,
  input  in_22,
  input  in_23,
  input  in_24,
  input  in_25,
  input  in_26,
  output out_27,
  output out_28,
  output out_29,
  output out_30,
  output out_31,
  output out_32,
  output out_33,
  output out_34,
  output out_35,
  output out_36,
  output out_37,
  output out_38,
  output out_39,
  output out_40,
  output out_41,
  output out_42,
  output out_43,
  output out_44,
  output out_45,
  output out_46,
  output out_47,
  output out_48,
  output out_49,
  output out_50,
  output out_51,
  output out_52,
  output out_53,
  output out_54,
  output out_55,
  output out_56,
  output out_57,
  output out_58,
  output out_59,
  output out_60,
  output out_61,
  output out_62,
  output out_63,
  output out_64,
  output out_65,
  output out_66,
  output out_67,
  output out_68,
  output out_69,
  output out_70,
  output out_71,
  output out_72,
  output out_73,
  output out_74,
  output out_75,
  output out_76,
  output out_77,
  output out_78,
  output out_79,
  output out_80,
  output out_81,
  output out_82
);

  wire and_1_out, and_2_out, and_3_out, and_4_out, and_5_out, and_6_out, and_7_out, clock_1_out, clock_2_out,
       clock_3_out, decoder_1_out0, decoder_1_out1, decoder_1_out2, decoder_1_out3, decoder_1_out4,
       decoder_1_out5, decoder_1_out6, decoder_1_out7, decoder_2_out0, decoder_2_out1, decoder_2_out2,
       decoder_2_out3, decoder_2_out4, decoder_2_out5, decoder_2_out6, decoder_2_out7, decoder_3_out0,
       decoder_3_out1, decoder_3_out2, decoder_3_out3, decoder_3_out4, decoder_3_out5, decoder_3_out6,
       decoder_3_out7, decoder_4_out0, decoder_4_out1, decoder_4_out2, decoder_4_out3, decoder_4_out4,
       decoder_4_out5, decoder_4_out6, decoder_4_out7, decoder_5_out0, decoder_5_out1, decoder_5_out2,
       decoder_5_out3, decoder_5_out4, decoder_5_out5, decoder_5_out6, decoder_5_out7, decoder_6_out0,
       decoder_6_out1, decoder_6_out2, decoder_6_out3, decoder_6_out4, decoder_6_out5, decoder_6_out6,
       decoder_6_out7, decoder_7_out0, decoder_7_out1, decoder_7_out2, decoder_7_out3, decoder_7_out4,
       decoder_7_out5, decoder_7_out6, decoder_7_out7;

  Clock clock_1 (.out(clock_1_out));
  Clock clock_2 (.out(clock_2_out));
  Decoder #(.select(3), .disabled(0)) decoder_1 (
    .out0(decoder_1_out0), .out1(decoder_1_out1), .out2(decoder_1_out2), .out3(decoder_1_out3),
    .out4(decoder_1_out4), .out5(decoder_1_out5), .out6(decoder_1_out6), .out7(decoder_1_out7),
    .sel({in_6, in_5, in_4}), .en(and_1_out));
  and and_1 (and_1_out, in_1, ~in_2, ~in_3);  // AND_Gate
  Decoder #(.select(3), .disabled(0)) decoder_2 (
    .out0(decoder_2_out0), .out1(decoder_2_out1), .out2(decoder_2_out2), .out3(decoder_2_out3),
    .out4(decoder_2_out4), .out5(decoder_2_out5), .out6(decoder_2_out6), .out7(decoder_2_out7), .sel(in_11),
    .en(and_2_out));
  and and_2 (and_2_out, clock_1_out, ~in_8, ~in_9);  // AND_Gate
  Decoder #(.select(3), .disabled(0)) decoder_3 (
    .out0(decoder_3_out0), .out1(decoder_3_out1), .out2(decoder_3_out2), .out3(decoder_3_out3),
    .out4(decoder_3_out4), .out5(decoder_3_out5), .out6(decoder_3_out6), .out7(decoder_3_out7),
    .sel({in_20, in_19, in_18}), .en(and_3_out));
  and and_3 (and_3_out, in_13, ~in_14, ~in_17);  // AND_Gate
  Decoder #(.select(3), .disabled(0)) decoder_4 (
    .out0(decoder_4_out0), .out1(decoder_4_out1), .out2(decoder_4_out2), .out3(decoder_4_out3),
    .out4(decoder_4_out4), .out5(decoder_4_out5), .out6(decoder_4_out6), .out7(decoder_4_out7),
    .sel({in_26, in_25, in_24}), .en(and_4_out));
  and and_4 (and_4_out, in_21, ~clock_2_out, ~in_23);  // AND_Gate
  not not_1 (out_27, decoder_1_out0);
  not not_2 (out_28, decoder_1_out1);
  not not_3 (out_29, decoder_1_out2);
  not not_4 (out_30, decoder_1_out3);
  not not_5 (out_31, decoder_1_out4);
  not not_6 (out_32, decoder_1_out5);
  not not_7 (out_33, decoder_1_out6);
  not not_8 (out_34, decoder_1_out7);
  not not_9 (out_35, decoder_2_out0);
  not not_10 (out_37, decoder_2_out1);
  not not_11 (out_39, decoder_2_out2);
  not not_12 (out_41, decoder_2_out3);
  not not_13 (out_43, decoder_2_out4);
  not not_14 (out_45, decoder_2_out5);
  not not_15 (out_47, decoder_2_out6);
  not not_16 (out_49, decoder_2_out7);
  not not_17 (out_51, decoder_3_out0);
  not not_18 (out_53, decoder_3_out1);
  not not_19 (out_55, decoder_3_out2);
  not not_20 (out_57, decoder_3_out3);
  not not_21 (out_59, decoder_3_out4);
  not not_22 (out_61, decoder_3_out5);
  not not_23 (out_63, decoder_3_out6);
  not not_24 (out_65, decoder_3_out7);
  not not_25 (out_67, decoder_4_out0);
  not not_26 (out_69, decoder_4_out1);
  not not_27 (out_71, decoder_4_out2);
  not not_28 (out_73, decoder_4_out3);
  not not_29 (out_75, decoder_4_out4);
  not not_30 (out_77, decoder_4_out5);
  not not_31 (out_79, decoder_4_out6);
  not not_32 (out_81, decoder_4_out7);
  and and_5 (and_5_out, in_17, ~in_15, ~in_16);  // AND_Gate
  and and_6 (and_6_out, in_23, ~clock_2_out, ~in_22);  // AND_Gate
  Clock clock_3 (.out(clock_3_out));
  Decoder #(.select(3), .disabled(0)) decoder_5 (
    .out0(decoder_5_out0), .out1(decoder_5_out1), .out2(decoder_5_out2), .out3(decoder_5_out3),
    .out4(decoder_5_out4), .out5(decoder_5_out5), .out6(decoder_5_out6), .out7(decoder_5_out7), .sel(in_12),
    .en(and_7_out));
  and and_7 (and_7_out, in_7, ~clock_3_out, ~in_10);  // AND_Gate
  Decoder #(.select(3), .disabled(0)) decoder_6 (
    .out0(decoder_6_out0), .out1(decoder_6_out1), .out2(decoder_6_out2), .out3(decoder_6_out3),
    .out4(decoder_6_out4), .out5(decoder_6_out5), .out6(decoder_6_out6), .out7(decoder_6_out7),
    .sel({in_20, in_19, in_18}), .en(and_5_out));
  Decoder #(.select(3), .disabled(0)) decoder_7 (
    .out0(decoder_7_out0), .out1(decoder_7_out1), .out2(decoder_7_out2), .out3(decoder_7_out3),
    .out4(decoder_7_out4), .out5(decoder_7_out5), .out6(decoder_7_out6), .out7(decoder_7_out7),
    .sel({in_26, in_25, in_24}), .en(and_6_out));
  not not_33 (out_36, decoder_5_out0);
  not not_34 (out_38, decoder_5_out1);
  not not_35 (out_40, decoder_5_out2);
  not not_36 (out_42, decoder_5_out3);
  not not_37 (out_44, decoder_5_out4);
  not not_38 (out_46, decoder_5_out5);
  not not_39 (out_48, decoder_5_out6);
  not not_40 (out_50, decoder_5_out7);
  not not_41 (out_52, decoder_6_out0);
  not not_42 (out_54, decoder_6_out1);
  not not_43 (out_56, decoder_6_out2);
  not not_44 (out_58, decoder_6_out3);
  not not_45 (out_60, decoder_6_out4);
  not not_46 (out_62, decoder_6_out5);
  not not_47 (out_64, decoder_6_out6);
  not not_48 (out_66, decoder_6_out7);
  not not_49 (out_68, decoder_7_out0);
  not not_50 (out_70, decoder_7_out1);
  not not_51 (out_72, decoder_7_out2);
  not not_52 (out_74, decoder_7_out3);
  not not_53 (out_76, decoder_7_out4);
  not not_54 (out_78, decoder_7_out5);
  not not_55 (out_80, decoder_7_out6);
  not not_56 (out_82, decoder_7_out7);

  // Notes on the sheet:
  //   DECODER
  //   DEMULTIPLEXER
  //   DEMULTIPLEXER 1/16
  //   DEMULTIPLEXER 1/16
endmodule
