// Logisim project coders.circ as structural Verilog: 7 circuits, main circuit decoder_2_bit
module decoder_2_bit (
  input  in_1,
  input  in_2,
  input  active,
  output out_4,
  output out_5,
  output out_6,
  output out_7
);

  wire and_1_out, and_2_out, and_3_out, and_4_out, not_1_out, not_2_out;

  not not_1 (not_1_out, in_1);
  not not_2 (not_2_out, in_2);
  and and_1 (and_1_out, not_1_out, not_2_out);
  and and_2 (and_2_out, in_2, not_1_out);
  and and_3 (and_3_out, not_2_out, in_1);
  and and_4 (and_4_out, in_2, in_1);
  and and_5 (out_4, active, and_1_out);
  and and_6 (out_5, active, and_2_out);
  and and_7 (out_6, active, and_3_out);
  and and_8 (out_7, active, and_4_out);
endmodule

module decoder_3_bit (
  input  in_1,
  input  in_2,
  input  in_3,
  output out_4,
  output out_5,
  output out_6,
  output out_7,
  output out_8,
  output out_9,
  output out_10,
  output out_11
);

  wire not_1_out;

  not not_1 (not_1_out, in_3);
  decoder_2_bit decoder_2_bit_1 (
    .in_1(in_2), .in_2(in_1), .active(not_1_out), .out_4(out_4), .out_5(out_5), .out_6(out_6), .out_7(out_7));
  decoder_2_bit decoder_2_bit_2 (
    .in_1(in_2), .in_2(in_1), .active(in_3), .out_4(out_8), .out_5(out_9), .out_6(out_10), .out_7(out_11));
endmodule

module sum_1_bit (
  input  in_1,
  input  in_2,
  input  in_3,
  output out_4,
  output out_5
);

  wire and_1_out, and_2_out, and_3_out, xor_1_out;

  xor xor_1 (xor_1_out, in_2, in_3);
  and and_1 (and_1_out, in_1, in_2);
  and and_2 (and_2_out, in_1, in_3);
  and and_3 (and_3_out, in_2, in_3);
  xor xor_2 (out_4, in_1, xor_1_out);
  or or_1 (out_5, and_1_out, and_2_out, and_3_out);
endmodule

module alu_1_bit (
  input  [2:0] ctrl,
  input  prev_carry,
  input  [1:0] in_3,
  output m_out,
  output s_out
);

  wire and_1_out, nand_1_out, nor_1_out, not_1_out, not_2_out, or_1_out, sum_1_bit_1_out_4, xor_1_out;

  sum_1_bit sum_1_bit_1 (.in_1(prev_carry), .in_2(in_3[0]), .in_3(in_3[1]), .out_4(sum_1_bit_1_out_4), .out_5(s_out));
  nand nand_1 (nand_1_out, in_3[0], in_3[1]);
  nor nor_1 (nor_1_out, in_3[0], in_3[1]);
  not not_1 (not_1_out, in_3[0]);
  not not_2 (not_2_out, in_3[1]);
  xor xor_1 (xor_1_out, in_3[0], in_3[1]);
  or or_1 (or_1_out, in_3[0], in_3[1]);
  and and_1 (and_1_out, in_3[0], in_3[1]);
  Multiplexer #(.select(3), .enable("false")) multiplexer_1 (
    .in0(nand_1_out), .in1(nor_1_out), .in2(not_1_out), .in3(not_2_out), .in4(xor_1_out), .in5(or_1_out),
    .in6(and_1_out), .in7(sum_1_bit_1_out_4), .out(m_out), .sel(ctrl));
endmodule

module alu_8_bit (
  input  [2:0] ctrl,
  input  prev_carry,
  input  [15:0] in_3,
  output [7:0] m_out,
  output s_out
);

  wire alu_1_bit_1_s_out, alu_1_bit_2_s_out, alu_1_bit_3_s_out, alu_1_bit_4_s_out, alu_1_bit_5_s_out,
       alu_1_bit_6_s_out, alu_1_bit_7_s_out;

  alu_1_bit alu_1_bit_1 (
    .ctrl(ctrl), .prev_carry(prev_carry), .in_3(in_3[1:0]), .m_out(m_out[0]), .s_out(alu_1_bit_1_s_out));
  alu_1_bit alu_1_bit_2 (
    .ctrl(ctrl), .prev_carry(alu_1_bit_1_s_out), .in_3(in_3[3:2]), .m_out(m_out[1]), .s_out(alu_1_bit_2_s_out));
  alu_1_bit alu_1_bit_3 (
    .ctrl(ctrl), .prev_carry(alu_1_bit_2_s_out), .in_3(in_3[5:4]), .m_out(m_out[2]), .s_out(alu_1_bit_3_s_out));
  alu_1_bit alu_1_bit_4 (
    .ctrl(ctrl), .prev_carry(alu_1_bit_3_s_out), .in_3(in_3[7:6]), .m_out(m_out[3]), .s_out(alu_1_bit_4_s_out));
  alu_1_bit alu_1_bit_5 (
    .ctrl(ctrl), .prev_carry(alu_1_bit_4_s_out), .in_3(in_3[9:8]), .m_out(m_out[4]), .s_out(alu_1_bit_5_s_out));
  alu_1_bit alu_1_bit_6 (
    .ctrl(ctrl), .prev_carry(alu_1_bit_5_s_out), .in_3(in_3[11:10]), .m_out(m_out[5]),
    .s_out(alu_1_bit_6_s_out));
  alu_1_bit alu_1_bit_7 (
    .ctrl(ctrl), .prev_carry(alu_1_bit_6_s_out), .in_3(in_3[13:12]), .m_out(m_out[6]),
    .s_out(alu_1_bit_7_s_out));
  alu_1_bit alu_1_bit_8 (
    .ctrl(ctrl), .prev_carry(alu_1_bit_7_s_out), .in_3(in_3[15:14]), .m_out(m_out[7]), .s_out(s_out));
endmodule

module alu_8_bit_splitted (
  input  [2:0] ctrl,
  input  [7:0] a,
  input  [7:0] b,
  output [7:0] m_out,
  output s_out
);

  alu_8_bit alu_8_bit_1 (
    .ctrl(ctrl), .prev_carry(1'b0),
    .in_3({b[7], a[7], b[6], a[6], b[5], a[5], b[4], a[4], b[3], a[3], b[2], a[2], b[1], a[1], b[0], a[0]}),
    .m_out(m_out), .s_out(s_out));
endmodule

module test (
  input  [2:0] in_1,
  input  [7:0] in_2,
  input  [7:0] in_3,
  output out_4,
  output [7:0] out_5
);

  alu_8_bit_splitted alu_8_bit_splitted_1 (.ctrl(in_1), .a(in_2), .b(in_3), .m_out(out_5), .s_out(out_4));
endmodule
