// Logisim project counters.circ as structural Verilog: 3 circuits, main circuit counter_up
module demult (
  input  in_1,
  input  in_2,
  input  in_3,
  input  in_4,
  output out_5,
  output out_6,
  output out_7,
  output out_8,
  output out_9,
  output out_10,
  output out_11,
  output out_12
);

  wire and_1_out, and_2_out, and_3_out, and_4_out, and_5_out, and_6_out, and_7_out, and_8_out, not_1_out,
       not_2_out, not_3_out;

  not not_1 (not_1_out, in_1);
  not not_2 (not_2_out, in_2);
  not not_3 (not_3_out, in_3);
  and and_1 (and_1_out, not_3_out, not_2_out, not_1_out);
  and and_2 (and_2_out, in_3, not_2_out, not_1_out);
  and and_3 (and_3_out, not_3_out, in_2, not_1_out);
  and and_4 (and_4_out, in_3, in_2, not_1_out);
  and and_5 (and_5_out, not_3_out, not_2_out, in_1);
  and and_6 (and_6_out, in_3, not_2_out, in_1);
  and and_7 (and_7_out, not_3_out, in_2, in_1);
  and and_8 (and_8_out, in_3, in_2, in_1);
  and and_9 (out_5, in_4, and_1_out);
  and and_10 (out_6, in_4, and_2_out);
  and and_11 (out_7, in_4, and_3_out);
  and and_12 (out_8, in_4, and_4_out);
  and and_13 (out_9, in_4, and_5_out);
  and and_14 (out_10, in_4, and_6_out);
  and and_15 (out_11, in_4, and_7_out);
  and and_16 (out_12, in_4, and_8_out);
endmodule

module counter_up (
  input  in_1,
  input  in_2,
  input  in_3,
  input  in_4,
  input  CLK,
  output out_6,
  output out_7,
  output out_8,
  output out_9
);

  wire and_1_out, xnor_1_out, xnor_2_out, xnor_3_out, xnor_4_out;

  T_Flip_Flop #(.trigger("falling")) t_ff_1 (.T(1'b1), .clk(CLK), .Q(out_6), .reset(and_1_out));  // open: Qn, preset
  xnor xnor_1 (xnor_1_out, in_1, out_6);
  T_Flip_Flop #(.trigger("falling")) t_ff_2 (.T(1'b1), .clk(out_6), .Q(out_7), .reset(and_1_out));  // open: Qn, preset
  xnor xnor_2 (xnor_2_out, in_2, out_7);
  T_Flip_Flop #(.trigger("falling")) t_ff_3 (.T(1'b1), .clk(out_7), .Q(out_8), .reset(and_1_out));  // open: Qn, preset
  and and_1 (and_1_out, xnor_1_out, xnor_2_out, xnor_3_out, xnor_4_out);
  xnor xnor_3 (xnor_3_out, in_3, out_8);
  T_Flip_Flop #(.trigger("falling")) t_ff_4 (.T(1'b1), .clk(out_8), .Q(out_9), .reset(and_1_out));  // open: Qn, preset
  xnor xnor_4 (xnor_4_out, in_4, out_9);
endmodule

module counter_down (
  input  in_1,
  input  in_2,
  input  in_3,
  input  in_4,
  input  in_5,
  output [3:0] out_6,
  output out_7,
  output out_8,
  output out_9,
  output out_10
);

  wire and_1_out, and_2_out, and_3_out, and_4_out, and_5_out, t_ff_5_q;

  T_Flip_Flop t_ff_1 (.T(1'b1), .clk(in_1), .Q(out_6[0]), .reset(and_1_out));  // open: Qn, preset
  and and_1 (and_1_out, ~in_2, and_3_out);  // AND_Gate
  T_Flip_Flop t_ff_2 (.T(1'b1), .clk(out_6[0]), .Q(out_6[1]), .reset(and_2_out));  // open: Qn, preset
  and and_2 (and_2_out, ~in_3, and_3_out);  // AND_Gate
  and and_3 (and_3_out, out_6[3], out_6[2], t_ff_5_q, out_6[1], out_6[0]);
  T_Flip_Flop t_ff_3 (.T(1'b1), .clk(out_6[1]), .Q(out_6[2]), .reset(and_4_out));  // open: Qn, preset
  and and_4 (and_4_out, ~in_4, and_3_out);  // AND_Gate
  T_Flip_Flop t_ff_4 (.T(1'b1), .clk(out_6[2]), .Q(out_6[3]), .reset(and_5_out));  // open: Qn, preset
  and and_5 (and_5_out, ~in_5, and_3_out);  // AND_Gate
  T_Flip_Flop t_ff_5 (.T(1'b1), .clk(out_6[3]), .Q(t_ff_5_q), .reset(and_3_out));  // open: Qn, preset

  assign out_7 = out_6[0];
  assign out_8 = out_6[1];
  assign out_9 = out_6[2];
  assign out_10 = out_6[3];

  // Notes on the sheet:
  //   ZLICZA W DOL. ZATRZASKIWANY ZBOCZEN OPADAJĄCYM
endmodule
