// Logisim project cpu24.circ as structural Verilog: 9 circuits, main circuit main_cpu
module main_cpu (
  input  RESET,
  input  ENABLE,
  input  CLK,
  output [23:0] CURR
);

  wire alu_1_halt, and_1_out, controlled_buffer_1_out;
  wire [7:0] code_1_instr;
  wire [23:0] alu_1_new_a, alu_1_new_b, alu_1_new_c, alu_1_new_mem, alu_1_new_mem_adr, alu_1_next_step,
       code_1_step, mem_1_adr, mem_1_data, regi_1_a, regi_1_b, regi_1_c;

  and and_1 (and_1_out, ENABLE, ~alu_1_halt);  // AND_Gate
  assign controlled_buffer_1_out = and_1_out ? CLK : 1'bz;  // Controlled_Buffer controlled_buffer_1
  regi regi_1 (
    .new_a(alu_1_new_a), .new_b(alu_1_new_b), .new_c(alu_1_new_c), .CLK(controlled_buffer_1_out),
    .RESET(RESET), .a(regi_1_a), .b(regi_1_b), .c(regi_1_c));
  // Probe on regi_1_c
  code code_1 (
    .NEXT_STEP(alu_1_next_step), .CLK(controlled_buffer_1_out), .RESET(RESET), .INSTR(code_1_instr),
    .STEP(code_1_step));
  alu alu_1 (
    .INSTR(code_1_instr), .MEM_ADR(mem_1_adr), .MEM(mem_1_data), .STEP(code_1_step), .a(regi_1_a),
    .b(regi_1_b), .c(regi_1_c), .HALT(alu_1_halt), .NEW_MEM_ADR(alu_1_new_mem_adr), .NEW_MEM(alu_1_new_mem),
    .NEXT_STEP(alu_1_next_step), .new_a(alu_1_new_a), .new_b(alu_1_new_b), .new_c(alu_1_new_c), .CURR(CURR));
  mem mem_1 (
    .NEW_ADR(alu_1_new_mem_adr), .NEW_DATA(alu_1_new_mem), .CLK(controlled_buffer_1_out), .RESET(RESET),
    .data(mem_1_data), .ADR(mem_1_adr));

  // Notes on the sheet:
  //   CPU 24 BITS
endmodule

module alu (
  input  [7:0] INSTR,
  input  [23:0] MEM_ADR,
  input  [23:0] MEM,
  input  [23:0] STEP,
  input  [23:0] a,
  input  [23:0] b,
  input  [23:0] c,
  output HALT,
  output [23:0] NEW_MEM_ADR,
  output [23:0] NEW_MEM,
  output [23:0] NEXT_STEP,
  output [23:0] new_a,
  output [23:0] new_b,
  output [23:0] new_c,
  output [23:0] CURR
);

  wire decoder_1_out1, decoder_1_out2, decoder_1_out3, decoder_1_out4, decoder_1_out5, decoder_1_out6,
       decoder_1_out7;
  wire [23:0] adder_1_out, if_gate_1_o, operator_2_o;

  if_gate if_gate_1 (.i(decoder_1_out2), .t(MEM), .e(a), .o(if_gate_1_o));
  operator operator_1 (.CTRL(INSTR[4:0]), .a(if_gate_1_o), .b(b), .c(c), .o(CURR));
  Decoder #(.select(3), .enable("false")) decoder_1 (
    .out0(HALT), .out1(decoder_1_out1), .out2(decoder_1_out2), .out3(decoder_1_out3), .out4(decoder_1_out4),
    .out5(decoder_1_out5), .out6(decoder_1_out6), .out7(decoder_1_out7), .sel(INSTR[7:5]));
  if_gate if_gate_2 (.i(decoder_1_out5), .t(CURR), .e(if_gate_1_o), .o(new_a));
  if_gate if_gate_3 (.i(decoder_1_out6), .t(CURR), .e(b), .o(new_b));
  if_gate if_gate_4 (.i(decoder_1_out7), .t(CURR), .e(c), .o(new_c));
  if_gate if_gate_5 (.i(decoder_1_out1), .t(CURR), .e(MEM_ADR), .o(NEW_MEM_ADR));
  operator operator_2 (.CTRL(INSTR[4:0]), .a(STEP), .b(if_gate_1_o), .c(b), .o(operator_2_o));
  Adder #(.width(24)) adder_1 (.a(STEP), .b(24'h1), .out(adder_1_out));  // open: cin, cout
  if_gate if_gate_6 (.i(decoder_1_out3), .t(CURR), .e(MEM), .o(NEW_MEM));
  if_gate if_gate_7 (.i(decoder_1_out4), .t(operator_2_o), .e(adder_1_out), .o(NEXT_STEP));
endmodule

module if_gate (
  input  i,
  input  [23:0] t,
  input  [23:0] e,
  output [23:0] o
);

  wire not_1_out;

  not not_1 (not_1_out, i);
  assign o = not_1_out ? e : 24'bz;  // Controlled_Buffer controlled_buffer_1
  assign o = i ? t : 24'bz;  // Controlled_Buffer controlled_buffer_2
endmodule

module if_gate_ex (
  input  [23:0] i,
  input  [23:0] t,
  input  [23:0] e,
  output [23:0] out_4
);

  wire comparator_1_eq, not_1_out;

  Comparator #(.width(24)) comparator_1 (.a({24{1'b0}}), .b(i), .eq(comparator_1_eq));  // open: gt, lt
  not not_1 (not_1_out, comparator_1_eq);
  assign out_4 = not_1_out ? t : 24'bz;  // Controlled_Buffer controlled_buffer_1
  assign out_4 = comparator_1_eq ? e : 24'bz;  // Controlled_Buffer controlled_buffer_2
endmodule

module operator (
  input  [4:0] CTRL,
  input  [23:0] a,
  input  [23:0] b,
  input  [23:0] c,
  output [23:0] o
);

  wire comparator_1_gt, comparator_2_eq, comparator_3_eq;
  wire [4:0] bit_extender_3_out, bitadder_1_out;
  wire [23:0] adder_1_out, adder_2_out, and_1_out, bit_extender_1_out, bit_extender_2_out,
       bit_extender_4_out, bit_extender_5_out, divider_1_rem, divider_2_out, if_gate_ex_1_out_4,
       if_gate_ex_2_out_4, multiplier_1_out, negator_1_out, not_1_out, or_1_out, shifter_1_out,
       subtractor_1_out, xor_1_out;

  if_gate_ex if_gate_ex_1 (.i(a), .t(b), .e(c), .out_4(if_gate_ex_1_out_4));
  if_gate_ex if_gate_ex_2 (.i(a), .t(b), .e({24{1'b0}}), .out_4(if_gate_ex_2_out_4));
  assign bit_extender_1_out = {{23{comparator_1_gt}}, comparator_1_gt};  // Bit_Extender bit_extender_1
  Comparator #(.width(24)) comparator_1 (.a(a), .b(b), .gt(comparator_1_gt));  // open: eq, lt
  Comparator #(.width(24)) comparator_2 (.a(a), .b(b), .eq(comparator_2_eq));  // open: gt, lt
  assign bit_extender_2_out = {{23{comparator_2_eq}}, comparator_2_eq};  // Bit_Extender bit_extender_2
  Bit_Extender #(.in_width(24), .out_width(5), .\type ("zero")) bit_extender_3 (.in(b), .out(bit_extender_3_out));
  Shifter #(.width(24)) shifter_1 (.in(a), .\dist (bit_extender_3_out), .out(shifter_1_out));
  assign xor_1_out = a ^ b;  // XOR_Gate xor_1, 24 bits wide
  assign or_1_out = a | b;  // OR_Gate or_1, 24 bits wide
  assign and_1_out = a & b;  // AND_Gate and_1, 24 bits wide
  Divider #(.width(24)) divider_1 (.a(a), .b(b), .rem(divider_1_rem));  // open: out, upper
  Divider #(.width(24)) divider_2 (.a(a), .b(b), .out(divider_2_out));  // open: upper, rem
  Multiplier #(.width(24)) multiplier_1 (.a(a), .b(b), .out(multiplier_1_out));  // open: cin, cout
  Subtractor #(.width(24)) subtractor_1 (.a(a), .b(b), .out(subtractor_1_out));  // open: bin, bout
  Adder #(.width(24)) adder_1 (.a(a), .b(b), .out(adder_1_out));  // open: cin, cout
  BitAdder #(.width(24)) bitadder_1 (.in0(a), .out(bitadder_1_out));
  assign bit_extender_4_out = {{19{1'b0}}, bitadder_1_out};  // Bit_Extender bit_extender_4
  Comparator #(.width(24)) comparator_3 (.a(a), .b(24'hf), .eq(comparator_3_eq));  // open: gt, lt
  assign bit_extender_5_out = {{23{comparator_3_eq}}, comparator_3_eq};  // Bit_Extender bit_extender_5
  Adder #(.width(24)) adder_2 (.a(a), .b(24'h1), .out(adder_2_out));  // open: cin, cout
  Negator #(.width(24)) negator_1 (.in(a), .out(negator_1_out));
  assign not_1_out = ~a;  // NOT_Gate not_1, 24 bits wide
  Multiplexer #(.select(5), .width(24), .enable("false")) multiplexer_1 (
    .in0({24{1'b0}}), .in1({24{1'b1}}), .in2(a), .in3(b), .in4(c), .in5(not_1_out), .in6(negator_1_out),
    .in7(adder_2_out), .in8(bit_extender_5_out), .in9(bit_extender_4_out), .in10(adder_1_out),
    .in11(subtractor_1_out), .in12(multiplier_1_out), .in13(divider_2_out), .in14(divider_1_rem),
    .in15(and_1_out), .in16(or_1_out), .in17(xor_1_out), .in18(shifter_1_out), .in19(bit_extender_2_out),
    .in20(bit_extender_1_out), .in21(if_gate_ex_2_out_4), .in22(if_gate_ex_1_out_4), .out(o), .sel(CTRL));  // open: in23, in24, in25, in26, in27, in28, in29, in30, in31
endmodule

module mem (
  input  [23:0] NEW_ADR,
  input  [23:0] NEW_DATA,
  input  CLK,
  input  RESET,
  output [23:0] data,
  output [23:0] ADR
);

  Register #(.width(24), .trigger("falling")) register_1 (.D(NEW_ADR), .clk(CLK), .Q(ADR), .clr(RESET));  // open: en
  RAM #(.addrWidth(24), .dataWidth(24), .trigger("falling"), .databus("bibus")) ram_1 (
    .addr(ADR), .we(1'b1), .oe(1'b1), .clk(CLK), .din(NEW_DATA), .dout(data));
endmodule

module code (
  input  [23:0] NEXT_STEP,
  input  CLK,
  input  RESET,
  output [7:0] INSTR,
  output [23:0] STEP
);

  Register #(.width(24), .trigger("falling")) register_1 (.D(NEXT_STEP), .clk(CLK), .Q(STEP), .clr(RESET));  // open: en
  ROM #(.addrWidth(24)) rom_1 (.addr(STEP), .data(INSTR));

  // Notes on the sheet:
  //   contents of rom_1 (hex, n*v repeats v):
  //   6*e7 ee 0 248*e7
endmodule

module regi (
  input  [23:0] new_a,
  input  [23:0] new_b,
  input  [23:0] new_c,
  input  CLK,
  input  RESET,
  output [23:0] a,
  output [23:0] b,
  output [23:0] c
);

  wire undriven;

  Register #(.width(24), .trigger("falling")) register_1 (.D(new_a), .clk(CLK), .Q(a), .clr(RESET));  // open: en
  Register #(.width(24), .trigger("falling")) register_2 (.D(new_b), .en(undriven), .clk(CLK), .Q(b), .clr(RESET));
  Register #(.width(24), .trigger("falling")) register_3 (.D(new_c), .clk(CLK), .Q(c), .clr(RESET));  // open: en
endmodule

module test (
  input  in_1,
  input  in_2
);

  wire clock_1_out;
  wire [23:0] main_cpu_1_curr;

  Clock clock_1 (.out(clock_1_out));
  main_cpu main_cpu_1 (.RESET(in_1), .ENABLE(in_2), .CLK(clock_1_out), .CURR(main_cpu_1_curr));
  // Probe on main_cpu_1_curr
endmodule
