// Logisim project cpu24.circ as structural Verilog: 12 circuits, main circuit main_cpu
module comp (
);

  wire clock_1_out, main_cpu_1_u2, main_cpu_1_u3, or_1_out, RESET_out;
  wire [6:0] bit_extender_1_out;
  wire [23:0] main_cpu_1_instr, main_cpu_1_step, main_cpu_1_temp, main_cpu_1_wt, register_1_q;

  Clock clock_1 (.out(clock_1_out));
  Button RESET (.out(RESET_out));
  main_cpu main_cpu_1 (
    .RESET(RESET_out), .ENABLE(1'b1), .CLK(clock_1_out), .K0(register_1_q), .INSTR(main_cpu_1_instr),
    .STEP(main_cpu_1_step), .TEMP(main_cpu_1_temp), .WT(main_cpu_1_wt), .U2(main_cpu_1_u2), .U3(main_cpu_1_u3));  // open: K1, K2, K3, S2, S3, S4, S5, P0, P1, P2, P3
  // Probe on main_cpu_1_instr
  // Probe on main_cpu_1_step
  // Probe on main_cpu_1_temp
  // Probe on main_cpu_1_wt
  Register #(.width(24)) register_1 (
    .D(main_cpu_1_wt), .clk(clock_1_out), .Q(register_1_q), .clr(RESET_out));  // open: en
  // Probe on bit_extender_1_out
  Bit_Extender #(.in_width(24), .out_width(7), .\type ("zero")) bit_extender_1 (
    .in(main_cpu_1_wt), .out(bit_extender_1_out));
  TTY tty_1 (.data(bit_extender_1_out), .clk(main_cpu_1_u2), .clr(or_1_out));  // open: we
  or or_1 (or_1_out, main_cpu_1_u3, RESET_out);
endmodule

module main_cpu (
  input  RESET,
  input  ENABLE,
  input  CLK,
  input  [23:0] K0,
  input  [23:0] K1,
  input  [23:0] K2,
  input  [23:0] K3,
  input  [23:0] S2,
  input  [23:0] S3,
  input  [23:0] S4,
  input  [23:0] S5,
  output [23:0] INSTR,
  output [23:0] STEP,
  output [23:0] TEMP,
  output [23:0] P0,
  output [23:0] P1,
  output [23:0] P2,
  output [23:0] P3,
  output [23:0] WT,
  output U2,
  output U3
);

  wire controlled_buffer_1_out, decoder_1_out1;
  wire [4:0] bit_extender_1_out, bit_extender_2_out, register_1_q;
  wire [23:0] alu2b_1_new_a, alu2b_1_new_b, alu2b_1_new_c, alu2b_1_new_mem_adr, alu2b_1_new_temp,
       alu2b_1_new_wt, alu2b_1_next_step, alu2b_1_r_out, alu2b_1_w_out, mem_1_adr, mem_1_data,
       multiplexer_1_out, regi_1_a, regi_1_b, regi_1_c, RT_R_q;

  assign controlled_buffer_1_out = ENABLE ? CLK : 1'bz;  // Controlled_Buffer controlled_buffer_1
  regi regi_1 (
    .new_a(alu2b_1_new_a), .new_b(alu2b_1_new_b), .new_c(alu2b_1_new_c), .CLK(controlled_buffer_1_out),
    .RESET(RESET), .a(regi_1_a), .b(regi_1_b), .c(regi_1_c));
  // Probe on regi_1_a
  Bit_Extender #(.in_width(24), .out_width(5)) bit_extender_1 (.in(alu2b_1_r_out), .out(bit_extender_1_out));
  // Probe on regi_1_b
  // Probe on regi_1_c
  // Probe on mem_1_adr
  Register #(.width(5), .trigger("falling")) register_1 (
    .D(bit_extender_1_out), .clk(controlled_buffer_1_out), .Q(register_1_q), .clr(RESET));  // open: en
  // Probe on mem_1_data
  // Probe on STEP
  Multiplexer #(.select(5), .width(24), .enable("false")) multiplexer_1 (
    .in0(RT_R_q), .in1(mem_1_data), .in2(S2), .in3(S3), .in4(S4), .in5(S5), .out(multiplexer_1_out),
    .sel(register_1_q));  // open: in6, in7, in8, in9, in10, in11, in12, in13, in14, in15, in16, in17, in18, in19, in20, in21, in22, in23, in24, in25, in26, in27, in28, in29, in30, in31
  Register #(.width(24), .trigger("falling")) RT_R (
    .D(multiplexer_1_out), .clk(controlled_buffer_1_out), .Q(RT_R_q), .clr(RESET));  // open: en
  Register #(.width(24), .trigger("falling")) TEMP_R (.D(alu2b_1_new_temp), .Q(TEMP));  // open: en, clk, clr
  code code_1 (.NEXT_STEP(alu2b_1_next_step), .CLK(controlled_buffer_1_out), .RESET(RESET), .INSTR(INSTR), .STEP(STEP));
  alu2b alu2b_1 (
    .INSTR(INSTR), .TEMP(TEMP), .A(regi_1_a), .B(regi_1_b), .C(regi_1_c), .STEP(STEP), .MEM_ADR(mem_1_adr),
    .K0(K0), .K1(K1), .K2(K2), .K3(K3), .WT(WT), .RT(multiplexer_1_out), .W_IN({24{1'b0}}),
    .R_IN({24{1'b0}}), .NEW_TEMP(alu2b_1_new_temp), .NEW_A(alu2b_1_new_a), .NEW_B(alu2b_1_new_b),
    .NEW_C(alu2b_1_new_c), .NEXT_STEP(alu2b_1_next_step), .NEW_MEM_ADR(alu2b_1_new_mem_adr), .P0(P0),
    .P1(P1), .P2(P2), .P3(P3), .NEW_WT(alu2b_1_new_wt), .W_OUT(alu2b_1_w_out), .R_OUT(alu2b_1_r_out));  // open: K4, K5, CURR, P4, P5, NEW_RT
  Register #(.width(24), .trigger("falling")) WT_R (
    .D(alu2b_1_new_wt), .clk(controlled_buffer_1_out), .Q(WT), .clr(RESET));  // open: en
  Bit_Extender #(.in_width(24), .out_width(5)) bit_extender_2 (.in(alu2b_1_w_out), .out(bit_extender_2_out));
  Decoder #(.select(5), .enable("false")) decoder_1 (
    .out1(decoder_1_out1), .out2(U2), .out3(U3), .sel(bit_extender_2_out));  // open: out0, out4, out5, out6, out7, out8, out9, out10, out11, out12, out13, out14, out15, out16, out17, out18, out19, out20, out21, out22, out23, out24, out25, out26, out27, out28, out29, out30, out31
  mem mem_1 (
    .NEW_ADR(alu2b_1_new_mem_adr), .WE(decoder_1_out1), .NEW_DATA(WT), .CLK(controlled_buffer_1_out),
    .RESET(RESET), .data(mem_1_data), .ADR(mem_1_adr));

  // Notes on the sheet:
  //   CPU 24 BITS
endmodule

module alu2b (
  input  [23:0] INSTR,
  input  [23:0] TEMP,
  input  [23:0] A,
  input  [23:0] B,
  input  [23:0] C,
  input  [23:0] STEP,
  input  [23:0] MEM_ADR,
  input  [23:0] K0,
  input  [23:0] K1,
  input  [23:0] K2,
  input  [23:0] K3,
  input  [23:0] K4,
  input  [23:0] K5,
  input  [23:0] WT,
  input  [23:0] RT,
  input  [23:0] W_IN,
  input  [23:0] R_IN,
  output [23:0] CURR,
  output [23:0] NEW_TEMP,
  output [23:0] NEW_A,
  output [23:0] NEW_B,
  output [23:0] NEW_C,
  output [23:0] NEXT_STEP,
  output [23:0] NEW_MEM_ADR,
  output [23:0] P0,
  output [23:0] P1,
  output [23:0] P2,
  output [23:0] P3,
  output [23:0] P4,
  output [23:0] P5,
  output [23:0] NEW_WT,
  output [23:0] NEW_RT,
  output [23:0] W_OUT,
  output [23:0] R_OUT
);

  wire [23:0] adder_1_out, and_1_out, multiplexer_1_out, multiplexer_2_out, multiplexer_3_out, operator_1_o;

  Adder #(.width(24)) adder_1 (.a(STEP), .b(24'h1), .out(adder_1_out));  // open: cin, cout
  Multiplexer #(.select(4), .width(24), .enable("false")) multiplexer_1 (
    .in0(TEMP), .in1(A), .in2(B), .in3(C), .in4(adder_1_out), .in5(MEM_ADR), .in6(K0), .in7(K1), .in8(K2),
    .in9(K3), .in10(K4), .in11(K5), .in12(WT), .in13(RT), .in14(W_IN), .in15(R_IN), .out(multiplexer_1_out),
    .sel(INSTR[11:8]));
  Multiplexer #(.select(4), .width(24), .enable("false")) multiplexer_2 (
    .in0(TEMP), .in1(A), .in2(B), .in3(C), .in4(adder_1_out), .in5(MEM_ADR), .in6(K0), .in7(K1), .in8(K2),
    .in9(K3), .in10(K4), .in11(K5), .in12(WT), .in13(RT), .in14(W_IN), .in15(R_IN), .out(multiplexer_2_out),
    .sel(INSTR[7:4]));
  Multiplexer #(.select(4), .width(24), .enable("false")) multiplexer_3 (
    .in0(TEMP), .in1(A), .in2(B), .in3(C), .in4(adder_1_out), .in5(MEM_ADR), .in6(K0), .in7(K1), .in8(K2),
    .in9(K3), .in10(K4), .in11(K5), .in12(WT), .in13(RT), .in14(W_IN), .in15(R_IN), .out(multiplexer_3_out),
    .sel(INSTR[3:0]));
  // Probe on operator_1_o
  operator operator_1 (
    .CTRL(INSTR[16:12]), .a(multiplexer_1_out), .b(multiplexer_2_out), .c(multiplexer_3_out), .o(operator_1_o));
  assign and_1_out = INSTR & 24'hfffff;  // AND_Gate and_1, 24 bits wide
  if_gate if_gate_1 (.i(INSTR[19]), .t(operator_1_o), .e(and_1_out), .o(CURR));
  router router_1 (
    .K0(TEMP), .in_2(A), .in_3(B), .in_4(C), .in_5(adder_1_out), .in_6(MEM_ADR), .in_7(K0), .in_8(K1),
    .in_9(K2), .in_10(K3), .in_11(K4), .in_12(K5), .in_13(WT), .in_14(RT), .in_15(W_IN), .in_16(R_IN),
    .OVERRIDE(CURR), .DEST(INSTR[23:20]), .P0(NEW_TEMP), .out_20(NEW_A), .out_21(NEW_B), .out_22(NEW_C),
    .out_23(NEXT_STEP), .out_24(NEW_MEM_ADR), .out_25(P0), .out_26(P1), .out_27(P2), .out_28(P3),
    .out_29(P4), .out_30(P5), .out_31(NEW_WT), .out_32(NEW_RT), .out_33(W_OUT), .P15(R_OUT));

  // Notes on the sheet:
  //   ALU2b
endmodule

module if_gate (
  input  i,
  input  [23:0] t,
  input  [23:0] e,
  output [23:0] o
);

  wire not_1_out;

  not not_1 (not_1_out, i);
  assign o = not_1_out ? e : 24'bz;  // Controlled_Buffer controlled_buffer_1
  assign o = i ? t : 24'bz;  // Controlled_Buffer controlled_buffer_2
endmodule

module if_gate_ex (
  input  [23:0] i,
  input  [23:0] t,
  input  [23:0] e,
  output [23:0] out_4
);

  wire comparator_1_eq, not_1_out;

  Comparator #(.width(24)) comparator_1 (.a({24{1'b0}}), .b(i), .eq(comparator_1_eq));  // open: gt, lt
  not not_1 (not_1_out, comparator_1_eq);
  assign out_4 = not_1_out ? t : 24'bz;  // Controlled_Buffer controlled_buffer_1
  assign out_4 = comparator_1_eq ? e : 24'bz;  // Controlled_Buffer controlled_buffer_2
endmodule

module operator (
  input  [4:0] CTRL,
  input  [23:0] a,
  input  [23:0] b,
  input  [23:0] c,
  output [23:0] o
);

  wire comparator_1_gt, comparator_2_eq;
  wire [4:0] bit_extender_3_out, bitadder_1_out;
  wire [23:0] adder_1_out, adder_2_out, and_1_out, bit_extender_1_out, bit_extender_2_out,
       bit_extender_4_out, divider_1_rem, divider_2_out, if_gate_ex_1_out_4, if_gate_ex_2_out_4,
       multiplier_1_out, negator_1_out, not_1_out, or_1_out, shifter_1_out, subtractor_1_out,
       subtractor_2_out, xor_1_out;

  if_gate_ex if_gate_ex_1 (.i(a), .t(b), .e(c), .out_4(if_gate_ex_1_out_4));
  Comparator #(.width(24)) comparator_1 (.a(a), .b(b), .gt(comparator_1_gt));  // open: eq, lt
  assign bit_extender_1_out = {{23{comparator_1_gt}}, comparator_1_gt};  // Bit_Extender bit_extender_1
  Comparator #(.width(24)) comparator_2 (.a(a), .b(b), .eq(comparator_2_eq));  // open: gt, lt
  assign bit_extender_2_out = {{23{comparator_2_eq}}, comparator_2_eq};  // Bit_Extender bit_extender_2
  Bit_Extender #(.in_width(24), .out_width(5), .\type ("zero")) bit_extender_3 (.in(b), .out(bit_extender_3_out));
  Shifter #(.width(24)) shifter_1 (.in(a), .\dist (bit_extender_3_out), .out(shifter_1_out));
  assign xor_1_out = a ^ b;  // XOR_Gate xor_1, 24 bits wide
  assign or_1_out = a | b;  // OR_Gate or_1, 24 bits wide
  assign and_1_out = a & b;  // AND_Gate and_1, 24 bits wide
  Divider #(.width(24)) divider_1 (.a(a), .b(b), .rem(divider_1_rem));  // open: out, upper
  Divider #(.width(24)) divider_2 (.a(a), .b(b), .out(divider_2_out));  // open: upper, rem
  Multiplier #(.width(24)) multiplier_1 (.a(a), .b(b), .out(multiplier_1_out));  // open: cin, cout
  Subtractor #(.width(24)) subtractor_1 (.a(a), .b(b), .out(subtractor_1_out));  // open: bin, bout
  Adder #(.width(24)) adder_1 (.a(a), .b(b), .out(adder_1_out));  // open: cin, cout
  BitAdder #(.width(24)) bitadder_1 (.in0(a), .out(bitadder_1_out));
  assign bit_extender_4_out = {{19{1'b0}}, bitadder_1_out};  // Bit_Extender bit_extender_4
  Subtractor #(.width(24)) subtractor_2 (.a(a), .b(24'h1), .out(subtractor_2_out));  // open: bin, bout
  Adder #(.width(24)) adder_2 (.a(a), .b(24'h1), .out(adder_2_out));  // open: cin, cout
  if_gate_ex if_gate_ex_2 (.i(a), .t({24{1'b0}}), .e({24{1'b1}}), .out_4(if_gate_ex_2_out_4));
  Negator #(.width(24)) negator_1 (.in(a), .out(negator_1_out));
  assign not_1_out = ~a;  // NOT_Gate not_1, 24 bits wide
  Multiplexer #(.select(5), .width(24), .enable("false")) multiplexer_1 (
    .in0({24{1'b0}}), .in1({24{1'b1}}), .in2(a), .in3(b), .in4(c), .in5(not_1_out), .in6(negator_1_out),
    .in7(if_gate_ex_2_out_4), .in8(adder_2_out), .in9(subtractor_2_out), .in10(bit_extender_4_out),
    .in11(adder_1_out), .in12(subtractor_1_out), .in13(multiplier_1_out), .in14(divider_2_out),
    .in15(divider_1_rem), .in16(and_1_out), .in17(or_1_out), .in18(xor_1_out), .in19(shifter_1_out),
    .in20(bit_extender_2_out), .in21(bit_extender_1_out), .in22(if_gate_ex_1_out_4), .out(o), .sel(CTRL));  // open: in23, in24, in25, in26, in27, in28, in29, in30, in31
endmodule

module mem (
  input  [23:0] NEW_ADR,
  input  WE,
  input  [23:0] NEW_DATA,
  input  CLK,
  input  RESET,
  output [23:0] data,
  output [23:0] ADR
);

  wire not_1_out;

  Register #(.width(24), .trigger("falling")) register_1 (.D(NEW_ADR), .clk(CLK), .Q(ADR), .clr(RESET));  // open: en
  not not_1 (not_1_out, WE);
  RAM #(.addrWidth(24), .dataWidth(24), .trigger("high"), .databus("bibus")) ram_1 (
    .addr(ADR), .we(WE), .oe(not_1_out), .din(NEW_DATA), .dout(data));
endmodule

module code (
  input  [23:0] NEXT_STEP,
  input  CLK,
  input  RESET,
  output [23:0] INSTR,
  output [23:0] STEP
);

  Register #(.width(24), .trigger("falling")) register_1 (.D(NEXT_STEP), .clk(CLK), .Q(STEP), .clr(RESET));  // open: en
  ROM #(.addrWidth(24), .dataWidth(24)) rom_1 (.addr(STEP), .data(INSTR));

  // Notes on the sheet:
  //   contents of rom_1 (hex, n*v repeats v):
  //   500005 c0006b e00001 500006 c00075 e00001 500007 c0006d e00001 500008 c0000a e00001 500005 f00001
  //   c82d00 e00002 500006 f00001 c82d00 e00002 500007 f00001 c82d00 e00002 500008 f00001 c82d00 e00002
  //   489400
endmodule

module regi (
  input  [23:0] new_a,
  input  [23:0] new_b,
  input  [23:0] new_c,
  input  CLK,
  input  RESET,
  output [23:0] a,
  output [23:0] b,
  output [23:0] c
);

  wire undriven;

  Register #(.width(24), .trigger("falling")) register_1 (.D(new_a), .clk(CLK), .Q(a), .clr(RESET));  // open: en
  Register #(.width(24), .trigger("falling")) register_2 (.D(new_b), .en(undriven), .clk(CLK), .Q(b), .clr(RESET));
  Register #(.width(24), .trigger("falling")) register_3 (.D(new_c), .clk(CLK), .Q(c), .clr(RESET));  // open: en
endmodule

module router (
  input  [23:0] K0,
  input  [23:0] in_2,
  input  [23:0] in_3,
  input  [23:0] in_4,
  input  [23:0] in_5,
  input  [23:0] in_6,
  input  [23:0] in_7,
  input  [23:0] in_8,
  input  [23:0] in_9,
  input  [23:0] in_10,
  input  [23:0] in_11,
  input  [23:0] in_12,
  input  [23:0] in_13,
  input  [23:0] in_14,
  input  [23:0] in_15,
  input  [23:0] in_16,
  input  [23:0] OVERRIDE,
  input  [3:0] DEST,
  output [23:0] P0,
  output [23:0] out_20,
  output [23:0] out_21,
  output [23:0] out_22,
  output [23:0] out_23,
  output [23:0] out_24,
  output [23:0] out_25,
  output [23:0] out_26,
  output [23:0] out_27,
  output [23:0] out_28,
  output [23:0] out_29,
  output [23:0] out_30,
  output [23:0] out_31,
  output [23:0] out_32,
  output [23:0] out_33,
  output [23:0] P15
);

  wire decoder_1_out0, decoder_1_out1, decoder_1_out2, decoder_1_out3, decoder_1_out4, decoder_1_out5,
       decoder_1_out6, decoder_1_out7, decoder_1_out8, decoder_1_out9, decoder_1_out10, decoder_1_out11,
       decoder_1_out12, decoder_1_out13, decoder_1_out14, decoder_1_out15, not_1_out, not_2_out, not_3_out,
       not_4_out, not_5_out, not_6_out, not_7_out, not_8_out, not_9_out, not_10_out, not_11_out, not_12_out,
       not_13_out, not_14_out, not_15_out, not_16_out;

  Decoder #(.select(4), .enable("false")) decoder_1 (
    .out0(decoder_1_out0), .out1(decoder_1_out1), .out2(decoder_1_out2), .out3(decoder_1_out3),
    .out4(decoder_1_out4), .out5(decoder_1_out5), .out6(decoder_1_out6), .out7(decoder_1_out7),
    .out8(decoder_1_out8), .out9(decoder_1_out9), .out10(decoder_1_out10), .out11(decoder_1_out11),
    .out12(decoder_1_out12), .out13(decoder_1_out13), .out14(decoder_1_out14), .out15(decoder_1_out15),
    .sel(DEST));
  not not_1 (not_1_out, decoder_1_out0);
  assign P0 = not_1_out ? K0 : 24'bz;  // Controlled_Buffer controlled_buffer_1
  not not_2 (not_2_out, decoder_1_out1);
  assign out_20 = not_2_out ? in_2 : 24'bz;  // Controlled_Buffer controlled_buffer_2
  not not_3 (not_3_out, decoder_1_out2);
  assign out_21 = not_3_out ? in_3 : 24'bz;  // Controlled_Buffer controlled_buffer_3
  not not_4 (not_4_out, decoder_1_out3);
  assign out_22 = not_4_out ? in_4 : 24'bz;  // Controlled_Buffer controlled_buffer_4
  not not_5 (not_5_out, decoder_1_out4);
  assign out_23 = not_5_out ? in_5 : 24'bz;  // Controlled_Buffer controlled_buffer_5
  not not_6 (not_6_out, decoder_1_out5);
  assign out_24 = not_6_out ? in_6 : 24'bz;  // Controlled_Buffer controlled_buffer_6
  not not_7 (not_7_out, decoder_1_out6);
  assign out_25 = not_7_out ? in_7 : 24'bz;  // Controlled_Buffer controlled_buffer_7
  not not_8 (not_8_out, decoder_1_out7);
  assign out_26 = not_8_out ? in_8 : 24'bz;  // Controlled_Buffer controlled_buffer_8
  not not_9 (not_9_out, decoder_1_out8);
  assign out_27 = not_9_out ? in_9 : 24'bz;  // Controlled_Buffer controlled_buffer_9
  not not_10 (not_10_out, decoder_1_out9);
  assign out_28 = not_10_out ? in_10 : 24'bz;  // Controlled_Buffer controlled_buffer_10
  not not_11 (not_11_out, decoder_1_out10);
  assign out_29 = not_11_out ? in_11 : 24'bz;  // Controlled_Buffer controlled_buffer_11
  not not_12 (not_12_out, decoder_1_out11);
  assign out_30 = not_12_out ? in_12 : 24'bz;  // Controlled_Buffer controlled_buffer_12
  not not_13 (not_13_out, decoder_1_out12);
  assign out_31 = not_13_out ? in_13 : 24'bz;  // Controlled_Buffer controlled_buffer_13
  not not_14 (not_14_out, decoder_1_out13);
  assign out_32 = not_14_out ? in_14 : 24'bz;  // Controlled_Buffer controlled_buffer_14
  not not_15 (not_15_out, decoder_1_out14);
  assign out_33 = not_15_out ? in_15 : 24'bz;  // Controlled_Buffer controlled_buffer_15
  not not_16 (not_16_out, decoder_1_out15);
  assign P15 = not_16_out ? in_16 : 24'bz;  // Controlled_Buffer controlled_buffer_16
  assign P0 = decoder_1_out0 ? OVERRIDE : 24'bz;  // Controlled_Buffer controlled_buffer_17
  assign out_20 = decoder_1_out1 ? OVERRIDE : 24'bz;  // Controlled_Buffer controlled_buffer_18
  assign out_21 = decoder_1_out2 ? OVERRIDE : 24'bz;  // Controlled_Buffer controlled_buffer_19
  assign out_22 = decoder_1_out3 ? OVERRIDE : 24'bz;  // Controlled_Buffer controlled_buffer_20
  assign out_23 = decoder_1_out4 ? OVERRIDE : 24'bz;  // Controlled_Buffer controlled_buffer_21
  assign out_24 = decoder_1_out5 ? OVERRIDE : 24'bz;  // Controlled_Buffer controlled_buffer_22
  assign out_25 = decoder_1_out6 ? OVERRIDE : 24'bz;  // Controlled_Buffer controlled_buffer_23
  assign out_26 = decoder_1_out7 ? OVERRIDE : 24'bz;  // Controlled_Buffer controlled_buffer_24
  assign out_27 = decoder_1_out8 ? OVERRIDE : 24'bz;  // Controlled_Buffer controlled_buffer_25
  assign out_28 = decoder_1_out9 ? OVERRIDE : 24'bz;  // Controlled_Buffer controlled_buffer_26
  assign out_29 = decoder_1_out10 ? OVERRIDE : 24'bz;  // Controlled_Buffer controlled_buffer_27
  assign out_30 = decoder_1_out11 ? OVERRIDE : 24'bz;  // Controlled_Buffer controlled_buffer_28
  assign out_31 = decoder_1_out12 ? OVERRIDE : 24'bz;  // Controlled_Buffer controlled_buffer_29
  assign out_32 = decoder_1_out13 ? OVERRIDE : 24'bz;  // Controlled_Buffer controlled_buffer_30
  assign out_33 = decoder_1_out14 ? OVERRIDE : 24'bz;  // Controlled_Buffer controlled_buffer_31
  assign P15 = decoder_1_out15 ? OVERRIDE : 24'bz;  // Controlled_Buffer controlled_buffer_32
endmodule

module test (
  input  [23:0] in_1,
  input  [23:0] in_2,
  input  [23:0] in_3,
  input  in_4,
  input  in_5
);

  wire clock_1_out, undriven, undriven_2;
  wire [6:0] counter_1_q;
  wire [19:0] bit_extender_1_out;
  wire [23:0] and_1_out, bit_extender_2_out, main_cpu_1_instr;

  Counter #(.width(7), .max('h7f)) counter_1 (
    .clk(clock_1_out), .Q(counter_1_q));  // open: clr, load, up, count, D, carry
  Clock clock_1 (.out(clock_1_out));
  main_cpu main_cpu_1 (
    .RESET(in_4), .ENABLE(in_5), .CLK(clock_1_out), .INSTR(main_cpu_1_instr));  // open: K0, K1, K2, K3, S2, S3, S4, S5, STEP, TEMP, P0, P1, P2, P3, WT, U2, U3
  // Probe on main_cpu_1_instr
  TTY tty_1 (.data(counter_1_q), .clk(clock_1_out), .we(undriven), .clr(undriven_2));
  Bit_Extender #(.in_width(24), .out_width(20), .\type ("zero")) bit_extender_1 (.in(in_1), .out(bit_extender_1_out));
  assign and_1_out = in_2 & in_3;  // AND_Gate and_1, 24 bits wide
  assign bit_extender_2_out = {{4{1'b0}}, bit_extender_1_out};  // Bit_Extender bit_extender_2
  // Probe on bit_extender_2_out
  // Probe on and_1_out
  alu2b alu2b_1 ();  // open: INSTR, TEMP, A, B, C, STEP, MEM_ADR, K0, K1, K2, K3, K4, K5, WT, RT, W_IN, R_IN, CURR, NEW_TEMP, NEW_A, NEW_B, NEW_C, NEXT_STEP, NEW_MEM_ADR, P0, P1, P2, P3, P4, P5, NEW_WT, NEW_RT, W_OUT, R_OUT
endmodule

module test2 (
);

  wire button_1_out, clock_1_out, main_cpu_1_u2;
  wire [23:0] main_cpu_1_wt;

  Clock clock_1 (.out(clock_1_out));
  Button button_1 (.out(button_1_out));
  main_cpu main_cpu_1 (
    .RESET(button_1_out), .ENABLE(1'b1), .CLK(clock_1_out), .WT(main_cpu_1_wt), .U2(main_cpu_1_u2));  // open: K0, K1, K2, K3, S2, S3, S4, S5, INSTR, STEP, TEMP, P0, P1, P2, P3, U3
  // Probe on main_cpu_1_wt
  // Probe on main_cpu_1_u2
endmodule
