// Logisim project flip_flops.circ as structural Verilog: 3 circuits, main circuit flip_flops_main
module flip_flops_main (
  input  in_1,
  input  in_2,
  input  in_3,
  input  in_4,
  input  in_5,
  input  in_6,
  input  in_7,
  input  in_8,
  output [31:0] out_9,
  output NOT_Q,
  output Q,
  output NOT_Q_2,
  output Q_2,
  output Q_3,
  output NOT_Q_3,
  output NOT_Q_4,
  output Q_4,
  output Q_5,
  output NOT_Q_5,
  output NOT_Q_6
);

  wire nand_3_out, nand_4_out, nand_7_out, nand_8_out, nor_3_out, nor_4_out, nor_7_out, nor_8_out, not_1_out,
       not_2_out, not_3_out, not_4_out;

  nand nand_1 (out_9[6], in_1, NOT_Q);
  nand nand_2 (NOT_Q, out_9[6], in_2);
  nor nor_1 (Q, in_3, NOT_Q_2);
  nor nor_2 (NOT_Q_2, Q, in_4);
  not not_1 (not_1_out, NOT_Q_4);
  not not_2 (not_2_out, NOT_Q_6);
  nor nor_3 (nor_3_out, NOT_Q_4, in_6);
  nor nor_4 (nor_4_out, in_6, not_1_out);
  nand nand_3 (nand_3_out, NOT_Q_6, in_8);
  nand nand_4 (nand_4_out, in_8, not_2_out);
  nor nor_5 (Q_2, nor_3_out, NOT_Q_3);
  nor nor_6 (NOT_Q_3, Q_2, nor_4_out);
  nand nand_5 (Q_4, nand_3_out, NOT_Q_5);
  nand nand_6 (NOT_Q_5, Q_4, nand_4_out);
  not not_3 (not_3_out, in_6);
  not not_4 (not_4_out, in_8);
  nor nor_7 (nor_7_out, Q_2, not_3_out);
  nor nor_8 (nor_8_out, not_3_out, NOT_Q_3);
  nand nand_7 (nand_7_out, Q_4, not_4_out);
  nand nand_8 (nand_8_out, not_4_out, NOT_Q_5);
  nor nor_9 (Q_3, nor_7_out, NOT_Q_4);
  nor nor_10 (NOT_Q_4, Q_3, nor_8_out);
  nand nand_9 (Q_5, nand_7_out, NOT_Q_6);
  nand nand_10 (NOT_Q_6, Q_5, nand_8_out);
  T_Flip_Flop t_ff_1 ();  // open: T, clk, Q, Qn, reset, preset

  assign out_9[5:0] = {6{out_9[6]}};
endmodule

module countt (
  input  in_1,
  input  in_2,
  input  in_3,
  output [2:0] out_4
);

  wire d_ff_1_q, d_ff_1_qn;

  D_Flip_Flop d_ff_1 (.D(in_2), .clk(in_3), .Q(d_ff_1_q), .Qn(d_ff_1_qn));  // open: preset, reset
  t_simple t_simple_1 (.in_1(in_1), .out_2(out_4[0]));
  t_simple t_simple_2 (.in_1(out_4[0]), .out_2(out_4[1]));
  t_simple t_simple_3 (.in_1(out_4[1]), .out_2(out_4[2]));
  // AND_Gate and_1 is placed but not wired
endmodule

module t_simple (
  input  in_1,
  output out_2
);

  T_Flip_Flop #(.trigger("falling")) t_ff_1 (.T(1'b1), .clk(in_1), .Q(out_2));  // open: Qn, reset, preset
endmodule
