// Logisim project mult.circ as structural Verilog: 14 circuits, main circuit mult_main_b
module main_test (
  input  [31:0] in_1,
  input  [31:0] in_2,
  input  [3:0] in_3,
  input  [3:0] in_4,
  input  [3:0] in_5,
  output [3:0] out_6,
  output [3:0] out_7
);

  assign out_6 = ~(in_3 & in_4);  // NAND_Gate nand_1, 4 bits wide
  Adder #(.width(4)) adder_1 (.a(out_6), .b(in_5), .out(out_7));  // open: cin, cout
  mult_8_bit_block mult_8_bit_block_1 (.b(in_1), .prev_num(in_2));  // open: a, out_4, out_5, out_6
endmodule

module mult_32_bit (
  input  [31:0] a,
  input  [31:0] b,
  output [31:0] out_3,
  output [31:0] out_4,
  output [31:0] result
);

  wire [31:0] mult_8_bit_block_1_out_4, mult_8_bit_block_1_out_5, mult_8_bit_block_1_out_6,
       mult_8_bit_block_2_out_4, mult_8_bit_block_2_out_5, mult_8_bit_block_2_out_6,
       mult_8_bit_block_3_out_4, mult_8_bit_block_3_out_5, mult_8_bit_block_3_out_6;

  mult_8_bit_block mult_8_bit_block_1 (
    .a(a), .b(b), .prev_num({32{1'b0}}), .out_4(mult_8_bit_block_1_out_4), .out_5(mult_8_bit_block_1_out_5),
    .out_6(mult_8_bit_block_1_out_6));
  mult_8_bit_block mult_8_bit_block_2 (
    .a(mult_8_bit_block_1_out_4), .b(mult_8_bit_block_1_out_5), .prev_num(mult_8_bit_block_1_out_6),
    .out_4(mult_8_bit_block_2_out_4), .out_5(mult_8_bit_block_2_out_5), .out_6(mult_8_bit_block_2_out_6));
  mult_8_bit_block mult_8_bit_block_3 (
    .a(mult_8_bit_block_2_out_4), .b(mult_8_bit_block_2_out_5), .prev_num(mult_8_bit_block_2_out_6),
    .out_4(mult_8_bit_block_3_out_4), .out_5(mult_8_bit_block_3_out_5), .out_6(mult_8_bit_block_3_out_6));
  mult_8_bit_block mult_8_bit_block_4 (
    .a(mult_8_bit_block_3_out_4), .b(mult_8_bit_block_3_out_5), .prev_num(mult_8_bit_block_3_out_6),
    .out_4(out_3), .out_5(out_4), .out_6(result));
endmodule

module mult_8_bit_block (
  input  [31:0] a,
  input  [31:0] b,
  input  [31:0] prev_num,
  output [31:0] out_4,
  output [31:0] out_5,
  output [31:0] out_6
);

  wire [31:0] mult_block_d2_1_out_4, mult_block_d2_1_out_5, mult_block_d2_1_out_6, mult_block_d2_2_out_4,
       mult_block_d2_2_out_5, mult_block_d2_2_out_6, mult_block_d2_3_out_4, mult_block_d2_3_out_5,
       mult_block_d2_3_out_6, mult_block_d2_4_out_4, mult_block_d2_4_out_5, mult_block_d2_4_out_6,
       mult_block_d2_5_out_4, mult_block_d2_5_out_5, mult_block_d2_5_out_6, mult_block_d2_6_out_4,
       mult_block_d2_6_out_5, mult_block_d2_6_out_6, mult_block_d2_7_out_4, mult_block_d2_7_out_5,
       mult_block_d2_7_out_6;

  mult_block_d2 mult_block_d2_1 (
    .in_1(a), .in_2(b), .in_3(prev_num), .out_4(mult_block_d2_1_out_4), .out_5(mult_block_d2_1_out_5),
    .out_6(mult_block_d2_1_out_6));
  mult_block_d2 mult_block_d2_2 (
    .in_1(mult_block_d2_1_out_4), .in_2(mult_block_d2_1_out_5), .in_3(mult_block_d2_1_out_6),
    .out_4(mult_block_d2_2_out_4), .out_5(mult_block_d2_2_out_5), .out_6(mult_block_d2_2_out_6));
  mult_block_d2 mult_block_d2_3 (
    .in_1(mult_block_d2_2_out_4), .in_2(mult_block_d2_2_out_5), .in_3(mult_block_d2_2_out_6),
    .out_4(mult_block_d2_3_out_4), .out_5(mult_block_d2_3_out_5), .out_6(mult_block_d2_3_out_6));
  mult_block_d2 mult_block_d2_4 (
    .in_1(mult_block_d2_3_out_4), .in_2(mult_block_d2_3_out_5), .in_3(mult_block_d2_3_out_6),
    .out_4(mult_block_d2_4_out_4), .out_5(mult_block_d2_4_out_5), .out_6(mult_block_d2_4_out_6));
  mult_block_d2 mult_block_d2_5 (
    .in_1(mult_block_d2_4_out_4), .in_2(mult_block_d2_4_out_5), .in_3(mult_block_d2_4_out_6),
    .out_4(mult_block_d2_5_out_4), .out_5(mult_block_d2_5_out_5), .out_6(mult_block_d2_5_out_6));
  mult_block_d2 mult_block_d2_6 (
    .in_1(mult_block_d2_5_out_4), .in_2(mult_block_d2_5_out_5), .in_3(mult_block_d2_5_out_6),
    .out_4(mult_block_d2_6_out_4), .out_5(mult_block_d2_6_out_5), .out_6(mult_block_d2_6_out_6));
  mult_block_d2 mult_block_d2_7 (
    .in_1(mult_block_d2_6_out_4), .in_2(mult_block_d2_6_out_5), .in_3(mult_block_d2_6_out_6),
    .out_4(mult_block_d2_7_out_4), .out_5(mult_block_d2_7_out_5), .out_6(mult_block_d2_7_out_6));
  mult_block_d2 mult_block_d2_8 (
    .in_1(mult_block_d2_7_out_4), .in_2(mult_block_d2_7_out_5), .in_3(mult_block_d2_7_out_6), .out_4(out_4),
    .out_5(out_5), .out_6(out_6));
endmodule

module mult_block_d2 (
  input  [31:0] in_1,
  input  [31:0] in_2,
  input  [31:0] in_3,
  output [31:0] out_4,
  output [31:0] out_5,
  output [31:0] out_6
);

  wire [31:0] adder_1_out, and_1_out, nand_1_out;

  assign nand_1_out = ~(in_1 & 32'h1);  // NAND_Gate nand_1, 32 bits wide
  Adder #(.width(32)) adder_1 (.a(nand_1_out), .b(32'h1), .out(adder_1_out));  // open: cin, cout
  Shifter #(.width(32)) shifter_1 (.in(in_2), .\dist (5'b00001), .out(out_5));
  assign and_1_out = adder_1_out & in_2;  // AND_Gate and_1, 32 bits wide
  Shifter #(.width(32), .shift("lr")) shifter_2 (.in(in_1), .\dist (5'b00001), .out(out_4));
  Adder #(.width(32)) adder_2 (.a(and_1_out), .b(in_3), .out(out_6));  // open: cin, cout
endmodule

module mult_block_d (
  input  [31:0] in_1,
  input  [31:0] in_2,
  input  [31:0] in_3,
  output [31:0] out_4,
  output [31:0] out_5,
  output [31:0] out_6
);

  wire [31:0] pull_resistor_1_node;

  Shifter #(.width(32)) shifter_1 (.in(in_2), .\dist (5'b00001), .out(out_5));
  Pull_Resistor pull_resistor_1 (.node(pull_resistor_1_node));
  assign pull_resistor_1_node = in_1[0] ? in_2 : 32'bz;  // Controlled_Buffer controlled_buffer_1
  Shifter #(.width(32), .shift("lr")) shifter_2 (.in(in_1), .\dist (5'b00001), .out(out_4));
  Adder #(.width(32)) adder_1 (.a(pull_resistor_1_node), .b(in_3), .out(out_6));  // open: cin, cout
endmodule

module mult_main_c (
  input  in_1,
  input  [7:0] x,
  output [2:0] out_3,
  output [7:0] out_4
);

  wire clock_1_out;
  wire [7:0] mult_block_c_1_next_num, mult_block_c_1_sh_a, mult_block_c_1_sh_b, mult_block_c_2_next_num,
       mult_block_c_2_sh_a, mult_block_c_2_sh_b, mult_block_c_3_next_num, mult_block_c_3_sh_a,
       mult_block_c_3_sh_b, mult_block_c_4_next_num, mult_block_c_4_sh_a, mult_block_c_4_sh_b,
       mult_block_c_5_next_num, mult_block_c_5_sh_a, mult_block_c_5_sh_b;

  Clock clock_1 (.out(clock_1_out));
  // countt countt_1: pin names not known; wires that end beside it: clock_1_out, out_3, in_1
  mult_block_c mult_block_c_1 (
    .a(x), .b({{5{1'b0}}, out_3}), .prev_num({8{1'b0}}), .sh_a(mult_block_c_1_sh_a),
    .sh_b(mult_block_c_1_sh_b), .next_num(mult_block_c_1_next_num));
  mult_block_c mult_block_c_2 (
    .a(mult_block_c_1_sh_a), .b(mult_block_c_1_sh_b), .prev_num(mult_block_c_1_next_num),
    .sh_a(mult_block_c_2_sh_a), .sh_b(mult_block_c_2_sh_b), .next_num(mult_block_c_2_next_num));
  mult_block_c mult_block_c_3 (
    .a(mult_block_c_2_sh_a), .b(mult_block_c_2_sh_b), .prev_num(mult_block_c_2_next_num),
    .sh_a(mult_block_c_3_sh_a), .sh_b(mult_block_c_3_sh_b), .next_num(mult_block_c_3_next_num));
  mult_block_c mult_block_c_4 (
    .a(mult_block_c_3_sh_a), .b(mult_block_c_3_sh_b), .prev_num(mult_block_c_3_next_num),
    .sh_a(mult_block_c_4_sh_a), .sh_b(mult_block_c_4_sh_b), .next_num(mult_block_c_4_next_num));
  mult_block_c mult_block_c_5 (
    .a(mult_block_c_4_sh_a), .b(mult_block_c_4_sh_b), .prev_num(mult_block_c_4_next_num),
    .sh_a(mult_block_c_5_sh_a), .sh_b(mult_block_c_5_sh_b), .next_num(mult_block_c_5_next_num));
  mult_block_c mult_block_c_6 (
    .a(mult_block_c_5_sh_a), .b(mult_block_c_5_sh_b), .prev_num(mult_block_c_5_next_num), .next_num(out_4));  // open: sh_a, sh_b
endmodule

module mult_block_c (
  input  [7:0] a,
  input  [7:0] b,
  input  [7:0] prev_num,
  output [7:0] sh_a,
  output [7:0] sh_b,
  output [7:0] next_num
);

  wire [7:0] pull_resistor_1_node;

  Shifter shifter_1 (.in(b), .\dist (3'b001), .out(sh_b));
  Pull_Resistor pull_resistor_1 (.node(pull_resistor_1_node));
  assign pull_resistor_1_node = a[0] ? b : 8'bz;  // Controlled_Buffer controlled_buffer_1
  Shifter #(.shift("lr")) shifter_2 (.in(a), .\dist (3'b001), .out(sh_a));
  Adder adder_1 (.a(pull_resistor_1_node), .b(prev_num), .out(next_num));  // open: cin, cout
endmodule

module mult_main_b (
  input  [1:0] in_1,
  output [2:0] out_2,
  output [7:0] out_3
);

  wire undriven;
  wire [7:0] mult_block_b_1_next_num, mult_block_b_1_sh_b, mult_block_b_2_sh_b;

  Clock clock_1 ();  // open: out
  countt countt_1 (.in_1(undriven), .out_4(out_2));  // open: in_2, in_3
  mult_block_b mult_block_b_1 (
    .enable(in_1[0]), .b({{5{1'b0}}, out_2}), .prev_num({8{1'b0}}), .sh_b(mult_block_b_1_sh_b),
    .next_num(mult_block_b_1_next_num));
  mult_block_b mult_block_b_2 (
    .enable(in_1[1]), .b(mult_block_b_1_sh_b), .prev_num(mult_block_b_1_next_num),
    .sh_b(mult_block_b_2_sh_b), .next_num(out_3));
endmodule

module mult_block_b (
  input  enable,
  input  [7:0] b,
  input  [7:0] prev_num,
  output [7:0] sh_b,
  output [7:0] next_num
);

  wire [7:0] controlled_buffer_1_out;

  Shifter shifter_1 (.in(b), .\dist (3'b001), .out(sh_b));
  assign controlled_buffer_1_out = enable ? b : 8'bz;  // Controlled_Buffer controlled_buffer_1
  Pull_Resistor pull_resistor_1 (.node(controlled_buffer_1_out));
  Adder adder_1 (.a(controlled_buffer_1_out), .b(prev_num), .out(next_num));  // open: cin, cout
endmodule

module shifter2 (
  input  enable,
  input  [2:0] sh,
  input  [2:0] a,
  output [7:0] sh_a
);

  wire [2:0] and_1_out;

  and and_1 (and_1_out[0], enable, sh[0]);
  and and_2 (and_1_out[1], enable, sh[1]);
  and and_3 (and_1_out[2], enable, sh[2]);
  Shifter shifter_1 (.in({{5{1'b0}}, a}), .\dist (and_1_out), .out(sh_a));
endmodule

module mult_block (
  input  enable,
  input  [7:0] prev_num,
  input  [2:0] sh,
  input  [2:0] a,
  output [7:0] next_num,
  output [2:0] nsh
);

  wire [7:0] shifter2_1_sh_a;

  add1_3_simplified add1_3_simplified_1 (.in_1(sh), .out_2(nsh));
  shifter2 shifter2_1 (.enable(enable), .sh(sh), .a(a), .sh_a(shifter2_1_sh_a));
  Adder adder_1 (.a(shifter2_1_sh_a), .b(prev_num), .out(next_num));  // open: cin, cout
endmodule

module add1_3_simplified (
  input  [2:0] in_1,
  output [2:0] out_2
);

  wire and_1_out, and_2_out;

  not not_1 (out_2[0], in_1[0]);
  and and_1 (and_1_out, in_1[0], in_1[1]);
  and and_2 (and_2_out, and_1_out, in_1[2]);
  xor xor_1 (out_2[1], in_1[0], in_1[1]);
  xor xor_2 (out_2[2], and_1_out, in_1[2]);
endmodule

module add1_3 (
  input  in_1,
  input  in_2,
  input  in_3,
  output out_4,
  output out_5,
  output out_6
);

  wire and_1_out, and_2_out, and_3_out, and_4_out, and_5_out, and_6_out, and_7_out, or_1_out, or_2_out,
       xor_2_out, xor_3_out;

  and and_1 (and_1_out, 1'b1, in_1);
  xor xor_1 (out_4, 1'b1, in_1);
  xor xor_2 (xor_2_out, in_2, 1'b0);
  and and_2 (and_2_out, and_1_out, in_2);
  and and_3 (and_3_out, and_1_out, 1'b0);
  and and_4 (and_4_out, in_2, 1'b0);
  xor xor_3 (xor_3_out, in_3, 1'b0);
  and and_5 (and_5_out, or_1_out, in_3);
  and and_6 (and_6_out, or_1_out, 1'b0);
  and and_7 (and_7_out, in_3, 1'b0);
  xor xor_4 (out_5, and_1_out, xor_2_out);
  or or_1 (or_1_out, and_2_out, and_3_out, and_4_out);
  xor xor_5 (out_6, or_1_out, xor_3_out);
  or or_2 (or_2_out, and_5_out, and_6_out, and_7_out);
endmodule

module aaa (
  output out_1,
  output out_2,
  output out_3,
  output out_4,
  output out_5,
  output out_6,
  output out_7,
  output out_8
);
endmodule
