// Logisim project mysak-17.circ as structural Verilog: 1 circuit, main circuit main
module main (
  input  in_1,
  input  in_2,
  input  C,
  input  B,
  input  A,
  input  C_2,
  input  B_2,
  input  A_2,
  input  C_3,
  input  B_3,
  input  A_3,
  output out_12,
  output out_13,
  output out_14,
  output out_15,
  output out_16,
  output out_17,
  output out_18,
  output out_19,
  output out_20
);

  wire _0_2_out, _0_3_out, _1_2_out, _1_3_out, _2_2_out, _2_3_out, _3_2_out, _3_3_out, _4_2_out, _4_3_out,
       clock_1_out, clock_2_out, clock_3_out, clock_4_out, clock_5_out, clock_6_out, clock_7_out,
       clock_8_out, clock_9_out, nand_5_out, nand_6_out, nand_7_out, nand_8_out, nand_9_out, nand_10_out,
       nor_2_out, nor_3_out, nor_4_out, nor_5_out, nor_6_out, nor_7_out, nor_8_out, nor_9_out, nor_10_out,
       nor_11_out, nor_12_out, nor_13_out, nor_14_out, nor_15_out, nor_16_out, nor_17_out, not_1_out,
       not_2_out, not_4_out, not_6_out, not_7_out, not_8_out, not_9_out, not_10_out, not_11_out;

  not not_1 (not_1_out, B);
  not not_2 (not_2_out, C);
  // NOT_Gate not_3 is placed but not wired
  // AND_Gate and_1 is placed but not wired
  not not_4 (not_4_out, A);
  // NOT_Gate not_5 is placed but not wired
  nand _0 (out_12, A, B, C);
  nand _1 (out_13, A, not_1_out, C);
  nand _2 (out_14, A, B, not_2_out);
  nand _3 (out_15, A, not_1_out, not_2_out);
  nand _4 (out_17, not_4_out, B, C);
  nand nand_1 (out_18, not_4_out, not_1_out, C);
  nand nand_2 (out_19, not_4_out, B, not_2_out);
  nand nand_3 (out_20, not_4_out, not_2_out);
  // NAND_Gate nand_4 is placed but not wired
  // OR_Gate or_1 is placed but not wired
  // NOR_Gate nor_1 is placed but not wired
  // XOR_Gate xor_1 is placed but not wired
  not not_6 (not_6_out, C_2);
  not not_7 (not_7_out, B_2);
  not not_8 (not_8_out, A_2);
  nand _0_2 (_0_2_out, not_8_out, not_6_out, not_7_out);
  nand _1_2 (_1_2_out, not_8_out, B_2, not_6_out);
  nand _2_2 (_2_2_out, not_8_out, not_7_out, C_2);
  nand _3_2 (_3_2_out, A_2, not_7_out, not_6_out);
  nand _4_2 (_4_2_out, A_2, B_2, not_6_out);
  nand nand_5 (nand_5_out, A_2, not_7_out, C_2);
  nand nand_6 (nand_6_out, A_2, B_2, not_6_out);
  nand nand_7 (nand_7_out, A_2, B_2, C_2);
  Clock clock_1 (.out(clock_1_out));
  nor nor_2 (nor_2_out, clock_1_out, _0_2_out);
  nor nor_3 (nor_3_out, clock_1_out, _1_2_out);
  nor nor_4 (nor_4_out, clock_1_out, _2_2_out);
  nor nor_5 (nor_5_out, clock_1_out, _3_2_out);
  nor nor_6 (nor_6_out, clock_1_out, _4_2_out);
  nor nor_7 (nor_7_out, clock_1_out, nand_5_out);
  nor nor_8 (nor_8_out, clock_1_out, nand_6_out);
  nor nor_9 (nor_9_out, clock_1_out, nand_7_out);
  not not_9 (not_9_out, C_3);
  not not_10 (not_10_out, A_3);
  not not_11 (not_11_out, B_3);
  nand _0_3 (_0_3_out, not_10_out, not_9_out, not_11_out);
  nand _1_3 (_1_3_out, not_10_out, B_3, not_9_out);
  nand _2_3 (_2_3_out, not_10_out, not_11_out, C_3);
  nand _3_3 (_3_3_out, A_3, not_11_out, not_9_out);
  nand _4_3 (_4_3_out, A_3, B_3, not_9_out);
  nand nand_8 (nand_8_out, A_3, not_11_out, C_3);
  nand nand_9 (nand_9_out, A_3, B_3, not_9_out);
  nand nand_10 (nand_10_out, A_3, B_3, C_3);
  Clock clock_2 (.out(clock_2_out));
  Clock #(.highDuration(2), .lowDuration(2)) clock_3 (.out(clock_3_out));
  Clock #(.highDuration(3), .lowDuration(3)) clock_4 (.out(clock_4_out));
  Clock #(.highDuration(4), .lowDuration(4)) clock_5 (.out(clock_5_out));
  Clock #(.highDuration(5), .lowDuration(5)) clock_6 (.out(clock_6_out));
  Clock #(.highDuration(6), .lowDuration(6)) clock_7 (.out(clock_7_out));
  Clock #(.highDuration(7), .lowDuration(7)) clock_8 (.out(clock_8_out));
  Clock #(.highDuration(8), .lowDuration(8)) clock_9 (.out(clock_9_out));
  nor nor_10 (nor_10_out, clock_2_out, _0_3_out);
  nor nor_11 (nor_11_out, clock_3_out, _1_3_out);
  nor nor_12 (nor_12_out, clock_4_out, _2_3_out);
  nor nor_13 (nor_13_out, clock_5_out, _3_3_out);
  nor nor_14 (nor_14_out, clock_6_out, _4_3_out);
  nor nor_15 (nor_15_out, clock_7_out, nand_8_out);
  nor nor_16 (nor_16_out, clock_8_out, nand_9_out);
  nor nor_17 (nor_17_out, clock_9_out, nand_10_out);
  or or_2 (out_16, nor_10_out, nor_11_out, nor_12_out, nor_13_out, nor_14_out, nor_15_out, nor_16_out, nor_17_out);
  Clock clock_10 ();  // open: out
endmodule
