// Logisim project proc.circ as structural Verilog: 6 circuits, main circuit alu
module cpu_main (
  input  [7:0] MAX_CLOCK,
  input  RESET_CLOCK,
  input  ENABLE
);

  wire alu_1_halt, and_1_out, clock_1_out, comparator_1_eq, controlled_buffer_1_out, counter_1_carry;
  wire [7:0] A_q, alu_1_new_a, alu_1_new_b, alu_1_new_r, B_q, counter_1_q, R_q, rom_1_data;

  Clock clock_1 (.out(clock_1_out));
  and and_1 (and_1_out, ~alu_1_halt, ENABLE);  // AND_Gate
  assign controlled_buffer_1_out = and_1_out ? clock_1_out : 1'bz;  // Controlled_Buffer controlled_buffer_1
  Counter #(.trigger("falling")) counter_1 (
    .clr(RESET_CLOCK), .load(comparator_1_eq), .up(1'b1), .clk(controlled_buffer_1_out), .D({8{1'b0}}),
    .carry(counter_1_carry), .Q(counter_1_q));  // open: count
  // Probe on counter_1_q
  Comparator comparator_1 (.a(MAX_CLOCK), .b(counter_1_q), .eq(comparator_1_eq));  // open: gt, lt
  // Probe on alu_1_new_r
  ROM rom_1 (.addr(counter_1_q), .data(rom_1_data));
  rewrite_8_bits A (.CLK(controlled_buffer_1_out), .D(alu_1_new_r), .Q(A_q));
  rewrite_8_bits B (.CLK(controlled_buffer_1_out), .D(alu_1_new_b), .Q(B_q));
  rewrite_8_bits R (.CLK(controlled_buffer_1_out), .D(alu_1_new_a), .Q(R_q));
  // Probe on A_q
  // Probe on B_q
  alu alu_1 (
    .CTRL(rom_1_data), .A(A_q), .B(B_q), .R(R_q), .HALT(alu_1_halt), .NEW_A(alu_1_new_a),
    .NEW_B(alu_1_new_b), .NEW_R(alu_1_new_r));
  // Probe on alu_1_new_r

  // Notes on the sheet:
  //   contents of rom_1 (hex, n*v repeats v):
  //   6*e7 ee 0 248*e7
endmodule

module alu (
  input  [7:0] CTRL,
  input  [7:0] A,
  input  [7:0] B,
  input  [7:0] R,
  output HALT,
  output [7:0] NEW_A,
  output [7:0] NEW_B,
  output [7:0] NEW_R
);

  wire [7:0] adder_1_out, and_1_out, divider_1_out, divider_2_rem, if_gate_ex_1_c, multiplexer_1_out,
       multiplier_1_out, negator_1_out, not_1_out, or_1_out, xor_1_out;

  if_gate_ex if_gate_ex_1 (.I(A), .T(B), .E({8{1'b0}}), .C(if_gate_ex_1_c));
  Adder adder_1 (.a(A), .b(B), .out(adder_1_out));  // open: cin, cout
  assign xor_1_out = A ^ B;  // XOR_Gate xor_1, 8 bits wide
  assign or_1_out = A | B;  // OR_Gate or_1, 8 bits wide
  Multiplier multiplier_1 (.a(A), .b(B), .out(multiplier_1_out));  // open: cin, cout
  Divider divider_1 (.a(A), .b(B), .out(divider_1_out));  // open: upper, rem
  Divider divider_2 (.a(A), .b(B), .rem(divider_2_rem));  // open: out, upper
  assign not_1_out = ~A;  // NOT_Gate not_1, 8 bits wide
  Negator negator_1 (.in(A), .out(negator_1_out));
  assign and_1_out = A & B;  // AND_Gate and_1, 8 bits wide
  Multiplexer #(.select(5), .width(8), .enable("false")) multiplexer_1 (
    .in1(adder_1_out), .in2(xor_1_out), .in3(or_1_out), .in4(multiplier_1_out), .in5(divider_1_out),
    .in6(divider_2_rem), .in7(not_1_out), .in8(negator_1_out), .in9(if_gate_ex_1_c), .in10(A), .in11(B),
    .in12(R), .in13(and_1_out), .in14({8{1'b0}}), .in15({8{1'b1}}), .out(multiplexer_1_out), .sel(CTRL[4:0]));  // open: in0, in16, in17, in18, in19, in20, in21, in22, in23, in24, in25, in26, in27, in28, in29, in30, in31
  nor nor_1 (HALT, CTRL[7], CTRL[6], CTRL[5], CTRL[4], CTRL[3], CTRL[2], CTRL[1], CTRL[0]);
  if_gate if_gate_1 (.I(CTRL[5]), .T(multiplexer_1_out), .E(A), .out_4(NEW_A));
  if_gate if_gate_2 (.I(CTRL[6]), .T(multiplexer_1_out), .E(B), .out_4(NEW_B));
  if_gate if_gate_3 (.I(CTRL[7]), .T(multiplexer_1_out), .E(R), .out_4(NEW_R));
endmodule

module if_gate_ex (
  input  [7:0] I,
  input  [7:0] T,
  input  [7:0] E,
  output [7:0] C
);

  wire not_1_out, or_1_out;

  or or_1 (or_1_out, I[0], I[1], I[2], I[3], I[4], I[5], I[6], I[7]);
  not not_1 (not_1_out, or_1_out);
  assign C = or_1_out ? T : 8'bz;  // Controlled_Buffer controlled_buffer_1
  assign C = not_1_out ? E : 8'bz;  // Controlled_Buffer controlled_buffer_2
endmodule

module if_gate (
  input  I,
  input  [7:0] T,
  input  [7:0] E,
  output [7:0] out_4
);

  wire not_1_out;

  not not_1 (not_1_out, I);
  assign out_4 = I ? T : 8'bz;  // Controlled_Buffer controlled_buffer_1
  assign out_4 = not_1_out ? E : 8'bz;  // Controlled_Buffer controlled_buffer_2
endmodule

module rewrite_8_bits (
  input  CLK,
  input  [7:0] D,
  output [7:0] Q
);

  D_Flip_Flop #(.trigger("falling")) d_ff_1 (.D(D[7]), .clk(CLK), .Q(Q[7]));  // open: Qn, preset, reset
  D_Flip_Flop #(.trigger("falling")) d_ff_2 (.D(D[6]), .clk(CLK), .Q(Q[6]));  // open: Qn, preset, reset
  D_Flip_Flop #(.trigger("falling")) d_ff_3 (.D(D[5]), .clk(CLK), .Q(Q[5]));  // open: Qn, preset, reset
  D_Flip_Flop #(.trigger("falling")) d_ff_4 (.D(D[4]), .clk(CLK), .Q(Q[4]));  // open: Qn, preset, reset
  D_Flip_Flop #(.trigger("falling")) d_ff_5 (.D(D[3]), .clk(CLK), .Q(Q[3]));  // open: Qn, preset, reset
  D_Flip_Flop #(.trigger("falling")) d_ff_6 (.D(D[2]), .clk(CLK), .Q(Q[2]));  // open: Qn, preset, reset
  D_Flip_Flop #(.trigger("falling")) d_ff_7 (.D(D[1]), .clk(CLK), .Q(Q[1]));  // open: Qn, preset, reset
  D_Flip_Flop #(.trigger("falling")) d_ff_8 (.D(D[0]), .clk(CLK), .Q(Q[0]));  // open: Qn, preset, reset
endmodule

module test (
);

  cpu_main cpu_main_1 ();  // open: MAX_CLOCK, RESET_CLOCK, ENABLE
endmodule
