// Logisim project przerzutniki.circ as structural Verilog: 2 circuits, main circuit main
module main (
);

  // AND_Gate and_1 is placed but not wired
  // OR_Gate or_1 is placed but not wired
  // NAND_Gate nand_1 is placed but not wired
  // NOR_Gate nor_1 is placed but not wired
endmodule

module rc (
  input  nS,
  input  nR,
  input  S,
  input  R,
  input  S_2,
  input  CLK,
  input  S_3,
  input  S_4,
  input  in_9,
  input  in_10,
  input  in_11,
  input  in_12,
  input  in_13,
  input  in_14,
  input  in_15,
  input  in_16,
  input  S_5,
  input  in_18,
  input  in_19,
  input  in_20,
  input  in_21,
  output Q,
  output nQ,
  output Q_2,
  output nQ_2,
  output Q_3,
  output Q_4,
  output Q_5,
  output Q_6,
  output nQ_3,
  output Q_7,
  output nQ_4,
  output out_33,
  output out_34,
  output Q_8,
  output nQ_5,
  output out_37,
  output out_38,
  output out_39,
  output out_40
);

  wire and_1_out, and_2_out, clock_1_out, clock_2_out, clock_3_out, clock_4_out, d_ff_4_qn, d_ff_6_q,
       d_ff_8_q, nand_1_out, nand_2_out, nand_3_out, nand_4_out, nand_5_out, nand_6_out, nand_7_out,
       nand_8_out, nand_15_out, nand_16_out, nand_17_out, nand_18_out, nand_19_out, nand_20_out, nand_21_out,
       nand_22_out, nor_1_out, not_1_out, not_2_out, not_3_out, not_4_out, not_5_out, s_r_ff_1_q,
       s_r_ff_1_qn, s_r_ff_2_q, s_r_ff_2_qn, s_r_ff_3_q, s_r_ff_3_qn, s_r_ff_4_q, s_r_ff_4_qn, s_r_ff_5_q,
       s_r_ff_5_qn;

  Clock clock_1 (.out(clock_1_out));
  not not_1 (not_1_out, S_2);
  Clock clock_2 (.out(clock_2_out));
  not not_2 (not_2_out, S_4);
  Clock clock_3 (.out(clock_3_out));
  not not_3 (not_3_out, S_5);
  Clock clock_4 (.out(clock_4_out));
  nand nand_1 (nand_1_out, S, clock_1_out);
  nand nand_2 (nand_2_out, clock_1_out, R);
  nand nand_3 (nand_3_out, S_2, clock_2_out);
  nand nand_4 (nand_4_out, clock_2_out, not_1_out);
  nand nand_5 (nand_5_out, S_4, clock_3_out);
  nand nand_6 (nand_6_out, clock_3_out, not_2_out);
  T_Flip_Flop t_ff_1 (.clk(in_13), .T(in_15), .Q(out_33));  // open: Qn, preset, reset, en
  nand nand_7 (nand_7_out, S_5, clock_4_out);
  nand nand_8 (nand_8_out, clock_4_out, not_3_out);
  D_Flip_Flop #(.trigger("falling")) d_ff_1 (.clk(in_21), .D(out_40), .Q(out_37));  // open: Qn, preset, en, reset
  D_Flip_Flop #(.trigger("falling")) d_ff_2 (.clk(in_21), .D(out_37), .Q(out_38));  // open: Qn, preset, en, reset
  nand nand_9 (Q, nS, nQ);
  nand nand_10 (nQ, Q, nR);
  nand nand_11 (Q_2, nand_1_out, nQ_2);
  nand nand_12 (nQ_2, Q_2, nand_2_out);
  nand nand_13 (Q_3, nand_3_out, nQ_3);
  nand nand_14 (nQ_3, Q_3, nand_4_out);
  nand nand_15 (nand_15_out, nand_5_out, nand_16_out);
  nand nand_16 (nand_16_out, nand_15_out, nand_6_out);
  nor nor_1 (nor_1_out, d_ff_4_qn, in_16);
  nand nand_17 (nand_17_out, nand_7_out, nand_18_out);
  nand nand_18 (nand_18_out, nand_17_out, nand_8_out);
  D_Flip_Flop #(.trigger("falling")) d_ff_3 (.clk(in_21), .D(out_38), .Q(out_39));  // open: Qn, preset, en, reset
  not not_4 (not_4_out, clock_3_out);
  D_Flip_Flop #(.trigger("low")) d_ff_4 (
    .clk(in_14), .D(nor_1_out), .Q(out_34), .Qn(d_ff_4_qn));  // open: preset, en, reset
  not not_5 (not_5_out, clock_4_out);
  D_Flip_Flop #(.trigger("falling")) d_ff_5 (.clk(in_21), .D(out_39), .Q(out_40));  // open: Qn, preset, en, reset
  nand nand_19 (nand_19_out, nand_15_out, not_4_out);
  nand nand_20 (nand_20_out, not_4_out, nand_16_out);
  nand nand_21 (nand_21_out, nand_17_out, not_5_out);
  nand nand_22 (nand_22_out, not_5_out, nand_18_out);
  D_Flip_Flop #(.trigger("low")) d_ff_6 (.clk(CLK), .D(S_3), .Q(d_ff_6_q), .Qn(Q_5));  // open: preset, en, reset
  nand nand_23 (Q_7, nand_19_out, nQ_4);
  nand nand_24 (nQ_4, Q_7, nand_20_out);
  S_R_Flip_Flop #(.trigger("high")) s_r_ff_1 (
    .S(s_r_ff_2_qn), .clk(in_11), .R(s_r_ff_2_q), .Q(s_r_ff_1_q), .Qn(s_r_ff_1_qn));  // open: preset, reset, en
  nand nand_25 (Q_8, nand_21_out, nQ_5);
  nand nand_26 (nQ_5, Q_8, nand_22_out);
  D_Flip_Flop #(.trigger("high")) d_ff_7 (.clk(CLK), .D(d_ff_6_q), .Q(Q_4), .Qn(Q_6));  // open: preset, en, reset
  S_R_Flip_Flop #(.trigger("low")) s_r_ff_2 (
    .S(s_r_ff_1_q), .clk(in_11), .R(s_r_ff_1_qn), .Q(s_r_ff_2_q), .Qn(s_r_ff_2_qn));  // open: preset, reset, en
  and and_1 (and_1_out, in_18, ~s_r_ff_4_q);  // AND_Gate
  and and_2 (and_2_out, in_20, ~s_r_ff_4_qn);  // AND_Gate
  S_R_Flip_Flop #(.trigger("falling")) s_r_ff_3 (
    .S(s_r_ff_3_qn), .clk(in_12), .R(s_r_ff_3_q), .Q(s_r_ff_3_q), .Qn(s_r_ff_3_qn));  // open: preset, reset, en
  S_R_Flip_Flop #(.trigger("falling")) s_r_ff_4 (
    .S(and_1_out), .clk(in_19), .R(and_2_out), .Q(s_r_ff_4_q), .Qn(s_r_ff_4_qn));  // open: preset, reset, en
  D_Flip_Flop #(.trigger("high")) d_ff_8 (.clk(in_9), .D(in_10), .Q(d_ff_8_q));  // open: Qn, preset, en, reset
  S_R_Flip_Flop #(.trigger("falling")) s_r_ff_5 (
    .S(s_r_ff_5_qn), .clk(d_ff_8_q), .R(s_r_ff_5_q), .Q(s_r_ff_5_q), .Qn(s_r_ff_5_qn));  // open: preset, reset, en
endmodule
