// Logisim project sumator_full.circ as structural Verilog: 7 circuits, main circuit full_1_bit
module addition (
  input  a0,
  input  b0,
  input  a1,
  input  b1,
  input  a2,
  input  b2,
  output _1,
  output _2,
  output _4,
  output _8
);

  wire and_1_out, and_2_out, and_3_out, and_4_out, and_5_out, and_6_out, and_7_out, and_8_out, and_9_out,
       or_1_out, or_2_out, xor_2_out, xor_3_out;

  xor xor_1 (_1, a0, b0);
  and and_1 (and_1_out, 1'b0, a0);
  and and_2 (and_2_out, 1'b0, b0);
  and and_3 (and_3_out, a0, b0);
  xor xor_2 (xor_2_out, a1, b1);
  and and_4 (and_4_out, or_1_out, a1);
  and and_5 (and_5_out, or_1_out, b1);
  and and_6 (and_6_out, a1, b1);
  xor xor_3 (xor_3_out, a2, b2);
  and and_7 (and_7_out, or_2_out, a2);
  and and_8 (and_8_out, or_2_out, b2);
  and and_9 (and_9_out, a2, b2);
  or or_1 (or_1_out, and_1_out, and_2_out, and_3_out);
  or or_2 (or_2_out, and_4_out, and_5_out, and_6_out);
  or or_3 (_8, and_7_out, and_8_out, and_9_out);
  xor xor_4 (_2, or_1_out, xor_2_out);
  xor xor_5 (_4, or_2_out, xor_3_out);
endmodule

module substraction (
  input  a0,
  input  b0,
  input  a1,
  input  b1,
  input  a2,
  input  b2,
  output _1,
  output _2,
  output _4,
  output _8
);

  wire and_1_out, and_2_out, and_3_out, and_4_out, and_5_out, and_6_out, and_7_out, and_8_out, and_9_out,
       or_1_out, or_2_out, xor_1_out, xor_2_out, xor_3_out, xor_4_out, xor_5_out, xor_6_out;

  xor xor_1 (xor_1_out, 1'b1, a0);
  xor xor_2 (xor_2_out, 1'b1, a1);
  xor xor_3 (xor_3_out, 1'b1, a2);
  xor xor_4 (xor_4_out, xor_1_out, b0);
  and and_1 (and_1_out, 1'b1, xor_1_out);
  and and_2 (and_2_out, 1'b1, b0);
  and and_3 (and_3_out, xor_1_out, b0);
  xor xor_5 (xor_5_out, xor_2_out, b1);
  and and_4 (and_4_out, or_1_out, xor_2_out);
  and and_5 (and_5_out, or_1_out, b1);
  and and_6 (and_6_out, xor_2_out, b1);
  xor xor_6 (xor_6_out, xor_3_out, b2);
  and and_7 (and_7_out, or_2_out, xor_3_out);
  and and_8 (and_8_out, or_2_out, b2);
  and and_9 (and_9_out, xor_3_out, b2);
  or or_1 (or_1_out, and_1_out, and_2_out, and_3_out);
  or or_2 (or_2_out, and_4_out, and_5_out, and_6_out);
  or or_3 (_8, and_7_out, and_8_out, and_9_out);
  xor xor_7 (_1, 1'b1, xor_4_out);
  xor xor_8 (_2, or_1_out, xor_5_out);
  xor xor_9 (_4, or_2_out, xor_6_out);

  // Notes on the sheet:
  //   if 1 then (b-a), otherwise (b+a)
endmodule

module full_1_bit (
  input  prev_carry,
  input  a,
  input  b,
  output sum,
  output carry
);

  wire and_1_out, and_2_out, and_3_out, xor_1_out;

  xor xor_1 (xor_1_out, a, b);
  and and_1 (and_1_out, prev_carry, a);
  and and_2 (and_2_out, prev_carry, b);
  and and_3 (and_3_out, a, b);
  or or_1 (carry, and_1_out, and_2_out, and_3_out);
  xor xor_2 (sum, prev_carry, xor_1_out);
endmodule

module full_8_bit (
  input  prev_carry,
  input  in_2,
  input  in_3,
  input  in_4,
  input  in_5,
  input  in_6,
  input  in_7,
  input  in_8,
  input  in_9,
  input  in_10,
  input  in_11,
  input  in_12,
  input  in_13,
  input  in_14,
  input  in_15,
  input  in_16,
  input  in_17,
  output out_18,
  output out_19,
  output out_20,
  output out_21,
  output out_22,
  output out_23,
  output out_24,
  output out_25,
  output carry
);

  wire full_1_bit_1_carry, full_1_bit_2_carry, full_1_bit_3_carry, full_1_bit_4_carry, full_1_bit_5_carry,
       full_1_bit_6_carry, full_1_bit_7_carry;

  full_1_bit full_1_bit_1 (.prev_carry(prev_carry), .a(in_2), .b(in_3), .sum(out_18), .carry(full_1_bit_1_carry));
  full_1_bit full_1_bit_2 (
    .prev_carry(full_1_bit_1_carry), .a(in_4), .b(in_5), .sum(out_19), .carry(full_1_bit_2_carry));
  full_1_bit full_1_bit_3 (
    .prev_carry(full_1_bit_2_carry), .a(in_6), .b(in_7), .sum(out_20), .carry(full_1_bit_3_carry));
  full_1_bit full_1_bit_4 (
    .prev_carry(full_1_bit_3_carry), .a(in_8), .b(in_9), .sum(out_21), .carry(full_1_bit_4_carry));
  full_1_bit full_1_bit_5 (
    .prev_carry(full_1_bit_4_carry), .a(in_10), .b(in_11), .sum(out_22), .carry(full_1_bit_5_carry));
  full_1_bit full_1_bit_6 (
    .prev_carry(full_1_bit_5_carry), .a(in_12), .b(in_13), .sum(out_23), .carry(full_1_bit_6_carry));
  full_1_bit full_1_bit_7 (
    .prev_carry(full_1_bit_6_carry), .a(in_14), .b(in_15), .sum(out_24), .carry(full_1_bit_7_carry));
  full_1_bit full_1_bit_8 (.prev_carry(full_1_bit_7_carry), .a(in_16), .b(in_17), .sum(out_25), .carry(carry));
endmodule

module full_32_bit (
  input  prev_carry,
  input  a0,
  input  b0,
  input  a1,
  input  b1,
  input  in_6,
  input  in_7,
  input  in_8,
  input  in_9,
  input  in_10,
  input  in_11,
  input  in_12,
  input  in_13,
  input  in_14,
  input  in_15,
  input  in_16,
  input  in_17,
  input  a8,
  input  b8,
  input  a9,
  input  b9,
  input  in_22,
  input  in_23,
  input  in_24,
  input  in_25,
  input  in_26,
  input  in_27,
  input  in_28,
  input  in_29,
  input  in_30,
  input  in_31,
  input  in_32,
  input  in_33,
  input  a16,
  input  b16,
  input  a17,
  input  b17,
  input  in_38,
  input  in_39,
  input  in_40,
  input  in_41,
  input  in_42,
  input  in_43,
  input  in_44,
  input  in_45,
  input  in_46,
  input  in_47,
  input  in_48,
  input  in_49,
  input  a24,
  input  b24,
  input  a25,
  input  b25,
  input  a26,
  input  b26,
  input  a27,
  input  b27,
  input  a28,
  input  b28,
  input  a29,
  input  b29,
  input  a30,
  input  b30,
  input  a31,
  input  b31,
  input  carry,
  output o0,
  output o1,
  output o2,
  output o3,
  output o4,
  output out_72,
  output out_73,
  output out_74,
  output o8,
  output o9,
  output o10,
  output o11,
  output o12,
  output out_80,
  output out_81,
  output out_82,
  output o16,
  output o17,
  output o18,
  output o19,
  output o20,
  output out_88,
  output out_89,
  output out_90,
  output out_91,
  output out_92,
  output out_93,
  output out_94,
  output out_95,
  output out_96,
  output o30,
  output o31
);

  wire full_8_bit_1_carry, full_8_bit_2_carry, full_8_bit_3_carry;

  full_8_bit full_8_bit_1 (
    .prev_carry(prev_carry), .in_2(a0), .in_3(b0), .in_4(a1), .in_5(b1), .in_6(in_6), .in_7(in_7),
    .in_8(in_8), .in_9(in_9), .in_10(in_10), .in_11(in_11), .in_12(in_12), .in_13(in_13), .in_14(in_14),
    .in_15(in_15), .in_16(in_16), .in_17(in_17), .out_18(o0), .out_19(o1), .out_20(o2), .out_21(o3),
    .out_22(o4), .out_23(out_72), .out_24(out_73), .out_25(out_74), .carry(full_8_bit_1_carry));
  full_8_bit full_8_bit_2 (
    .prev_carry(full_8_bit_1_carry), .in_2(a8), .in_3(b8), .in_4(a9), .in_5(b9), .in_6(in_22), .in_7(in_23),
    .in_8(in_24), .in_9(in_25), .in_10(in_26), .in_11(in_27), .in_12(in_28), .in_13(in_29), .in_14(in_30),
    .in_15(in_31), .in_16(in_32), .in_17(in_33), .out_18(o8), .out_19(o9), .out_20(o10), .out_21(o11),
    .out_22(o12), .out_23(out_80), .out_24(out_81), .out_25(out_82), .carry(full_8_bit_2_carry));
  full_8_bit full_8_bit_3 (
    .prev_carry(full_8_bit_2_carry), .in_2(a16), .in_3(b16), .in_4(a17), .in_5(b17), .in_6(in_38),
    .in_7(in_39), .in_8(in_40), .in_9(in_41), .in_10(in_42), .in_11(in_43), .in_12(in_44), .in_13(in_45),
    .in_14(in_46), .in_15(in_47), .in_16(in_48), .in_17(in_49), .out_18(o16), .out_19(o17), .out_20(o18),
    .out_21(o19), .out_22(o20), .out_23(out_88), .out_24(out_89), .out_25(out_90), .carry(full_8_bit_3_carry));
  full_8_bit full_8_bit_4 (
    .prev_carry(full_8_bit_3_carry), .in_2(a24), .in_3(b24), .in_4(a25), .in_5(b25), .in_6(a26), .in_7(b26),
    .in_8(a27), .in_9(b27), .in_10(a28), .in_11(b28), .in_12(a29), .in_13(b29), .in_14(a30), .in_15(b30),
    .in_16(a31), .in_17(b31), .out_18(out_91), .out_19(out_92), .out_20(out_93), .out_21(out_94),
    .out_22(out_95), .out_23(out_96), .out_24(o30), .out_25(o31), .carry(carry));
endmodule

module full_32_bit_splitted (
  input  [31:0] a,
  input  [31:0] b,
  output [31:0] result
);

  full_32_bit full_32_bit_1 (
    .prev_carry(1'b0), .a0(b[0]), .b0(a[0]), .a1(b[1]), .b1(a[1]), .in_6(b[2]), .in_7(a[2]), .in_8(b[3]),
    .in_9(a[3]), .in_10(b[4]), .in_11(a[4]), .in_12(b[5]), .in_13(a[5]), .in_14(b[6]), .in_15(a[6]),
    .in_16(b[7]), .in_17(a[7]), .a8(b[8]), .b8(a[8]), .a9(b[9]), .b9(a[9]), .in_22(b[10]), .in_23(a[10]),
    .in_24(b[11]), .in_25(a[11]), .in_26(b[12]), .in_27(a[12]), .in_28(b[13]), .in_29(a[13]), .in_30(b[14]),
    .in_31(a[14]), .in_32(b[15]), .in_33(a[15]), .a16(b[16]), .b16(a[16]), .a17(b[17]), .b17(a[17]),
    .in_38(b[18]), .in_39(a[18]), .in_40(b[19]), .in_41(a[19]), .in_42(b[20]), .in_43(a[20]), .in_44(b[21]),
    .in_45(a[21]), .in_46(b[22]), .in_47(a[22]), .in_48(b[23]), .in_49(a[23]), .a24(b[24]), .b24(a[24]),
    .a25(b[25]), .b25(a[25]), .a26(b[26]), .b26(a[26]), .a27(b[27]), .b27(a[27]), .a28(b[28]), .b28(a[28]),
    .a29(b[29]), .b29(a[29]), .a30(b[30]), .b30(a[30]), .a31(b[31]), .b31(a[31]), .o0(result[0]),
    .o1(result[1]), .o2(result[2]), .o3(result[3]), .o4(result[4]), .out_72(result[5]), .out_73(result[6]),
    .out_74(result[7]), .o8(result[8]), .o9(result[9]), .o10(result[10]), .o11(result[11]), .o12(result[12]),
    .out_80(result[13]), .out_81(result[14]), .out_82(result[15]), .o16(result[16]), .o17(result[17]),
    .o18(result[18]), .o19(result[19]), .o20(result[20]), .out_88(result[21]), .out_89(result[22]),
    .out_90(result[23]), .out_91(result[24]), .out_92(result[25]), .out_93(result[26]), .out_94(result[27]),
    .out_95(result[28]), .out_96(result[29]), .o30(result[30]), .o31(result[31]));  // open: carry
endmodule

module test (
  input  [31:0] in_1,
  input  [31:0] in_2,
  output [31:0] out_3
);

  full_32_bit_splitted full_32_bit_splitted_1 (.a(in_1), .b(in_2), .result(out_3));
endmodule
